// Logisim project лаба4.circ as structural Verilog: 16 circuits, main circuit rs-триггер
module \rs_триггер  (
  input  \input ,
  input  reset,
  output \output 
);

  wire not_1_out, or_1_out, or_2_out;

  or or_1 (or_1_out, \input , \output );
  or or_2 (or_2_out, not_1_out, reset);
  not not_1 (not_1_out, or_1_out);
  not not_2 (\output , or_2_out);
endmodule

module \d_триггер__разные  (
  input  in_1,
  input  data,
  input  clock,
  input  data_2,
  input  in_5,
  input  clock_2,
  input  data_3,
  input  data_4,
  input  clock_3,
  input  DATA_5,
  input  CLOCK_4,
  output \output ,
  output output_2,
  output output_3,
  output output_4,
  output minus_output,
  output OUTPUT_5,
  output minus_OUTPUT_2
);

  wire and_1_out, and_2_out, and_3_out, and_4_out, and_5_out, and_6_out, and_7_out, and_8_out, and_9_out,
       and_10_out, and_11_out, and_12_out, and_13_out, and_14_out, and_15_out, and_16_out, and_17_out,
       and_18_out, nor_1_out, nor_2_out, nor_3_out, nor_6_out, nor_7_out, not_1_out, not_2_out, not_3_out,
       not_4_out, not_5_out, not_6_out, not_7_out, not_8_out, not_9_out, not_10_out, not_11_out, not_12_out,
       not_13_out, not_14_out, not_15_out, or_1_out;

  not not_1 (not_1_out, data_3);
  not not_2 (not_2_out, data);
  not not_3 (not_3_out, data_2);
  not not_4 (not_4_out, clock);
  and and_1 (and_1_out, not_1_out, clock_2);
  and and_2 (and_2_out, data_4, not_5_out);
  not not_5 (not_5_out, clock_3);
  not not_6 (not_6_out, data_4);
  not not_7 (not_7_out, DATA_5);
  and and_3 (and_3_out, not_2_out, in_1);
  and and_4 (and_4_out, not_3_out, not_4_out);
  and and_5 (and_5_out, not_4_out, data_2);
  and and_6 (and_6_out, clock_2, data_3);
  and and_7 (and_7_out, not_5_out, not_6_out);
  and and_8 (and_8_out, DATA_5, CLOCK_4);
  not not_8 (not_8_out, and_8_out);
  and and_9 (and_9_out, CLOCK_4, not_7_out);
  not not_9 (not_9_out, and_9_out);
  and and_10 (and_10_out, in_1, data);
  or or_1 (or_1_out, in_5, and_1_out);
  nor nor_1 (nor_1_out, output_3, and_6_out);
  nor nor_2 (nor_2_out, and_2_out, nor_3_out);
  nor nor_3 (nor_3_out, nor_2_out, and_7_out);
  and and_11 (and_11_out, not_8_out, not_11_out);
  and and_12 (and_12_out, not_10_out, not_9_out);
  nor nor_4 (\output , and_3_out, nor_7_out);
  nor nor_5 (output_2, and_4_out, nor_6_out);
  nor nor_6 (nor_6_out, output_2, and_5_out);
  not not_10 (not_10_out, and_11_out);
  not not_11 (not_11_out, and_12_out);
  not not_12 (not_12_out, CLOCK_4);
  nor nor_7 (nor_7_out, \output , and_10_out);
  nor nor_8 (output_3, or_1_out, nor_1_out);
  and and_13 (and_13_out, nor_2_out, clock_3);
  and and_14 (and_14_out, clock_3, nor_3_out);
  and and_15 (and_15_out, not_10_out, not_12_out);
  and and_16 (and_16_out, not_12_out, not_13_out);
  not not_13 (not_13_out, not_10_out);
  not not_14 (not_14_out, and_15_out);
  not not_15 (not_15_out, and_16_out);
  nor nor_9 (output_4, and_13_out, minus_output);
  nor nor_10 (minus_output, output_4, and_14_out);
  and and_17 (and_17_out, not_14_out, minus_OUTPUT_2);
  not not_16 (OUTPUT_5, and_17_out);
  not not_17 (minus_OUTPUT_2, and_18_out);
  and and_18 (and_18_out, OUTPUT_5, not_15_out);

  // Notes on the sheet:
  //   clock
  //   clear
  //   HIGH LEVEL
  //   DOWN LEVEL
  //   ОЧИСТКА И ПРЕДУСТАНОВКА
  //   PEREDNIY FRONT
  //   ZADNIY FRONT
endmodule

module \T_триггер  (
  input  in_1,
  output out_2
);

  wire d_ff_1_qn;

  D_Flip_Flop d_ff_1 (.clk(in_1), .D(d_ff_1_qn), .Q(out_2), .Qn(d_ff_1_qn));  // open: preset, en, reset
endmodule

module \счетчик  (
  input  invert,
  input  [3:0] \input ,
  input  forward,
  input  clear,
  output [3:0] \output ,
  output \переполнение 
);

  wire clock_1_out;

  Clock clock_1 (.out(clock_1_out));
  Counter #(.width(4), .max('hf)) counter_1 (
    .load(invert), .D(\input ), .count(forward), .Q(\output ), .carry(\переполнение ), .clk(clock_1_out),
    .clr(clear));
endmodule

module \счетчик__нужный  (
  output out_1,
  output out_2,
  output out_3
);

  wire button_1_out, d_ff_1_qn, d_ff_2_qn, d_ff_3_qn;

  Button button_1 (.out(button_1_out));
  D_Flip_Flop d_ff_1 (.clk(button_1_out), .D(d_ff_1_qn), .Q(out_3), .Qn(d_ff_1_qn));  // open: preset, en, reset
  D_Flip_Flop d_ff_2 (.clk(d_ff_1_qn), .D(d_ff_2_qn), .Q(out_2), .Qn(d_ff_2_qn));  // open: preset, en, reset
  D_Flip_Flop d_ff_3 (.clk(d_ff_2_qn), .D(d_ff_3_qn), .Q(out_1), .Qn(d_ff_3_qn));  // open: preset, en, reset
endmodule

module \регистр  (
  input  clear,
  input  [7:0] in_2,
  input  in_3,
  input  clear_2,
  input  [7:0] in_5,
  output [7:0] out_6,
  output [7:0] out_7
);

  wire clock_1_out, clock_2_out;

  Clock clock_1 (.out(clock_1_out));
  Clock clock_2 (.out(clock_2_out));
  D_Flip_Flop d_ff_1 (.clk(clock_1_out), .D(in_2[0]), .Q(out_6[0]), .en(in_3), .reset(clear));  // open: Qn, preset
  D_Flip_Flop d_ff_2 (.clk(clock_1_out), .D(in_2[1]), .Q(out_6[1]), .en(in_3), .reset(clear));  // open: Qn, preset
  D_Flip_Flop d_ff_3 (.clk(clock_1_out), .D(in_2[2]), .Q(out_6[2]), .en(in_3), .reset(clear));  // open: Qn, preset
  D_Flip_Flop d_ff_4 (.clk(clock_1_out), .D(in_2[3]), .Q(out_6[3]), .en(in_3), .reset(clear));  // open: Qn, preset
  D_Flip_Flop d_ff_5 (.clk(clock_1_out), .D(in_2[4]), .Q(out_6[4]), .en(in_3), .reset(clear));  // open: Qn, preset
  D_Flip_Flop d_ff_6 (.clk(clock_1_out), .D(in_2[5]), .Q(out_6[5]), .en(in_3), .reset(clear));  // open: Qn, preset
  D_Flip_Flop d_ff_7 (.clk(clock_1_out), .D(in_2[6]), .Q(out_6[6]), .en(in_3), .reset(clear));  // open: Qn, preset
  D_Flip_Flop d_ff_8 (.clk(clock_1_out), .D(in_2[7]), .Q(out_6[7]), .en(in_3), .reset(clear));  // open: Qn, preset
  D_Flip_Flop d_ff_9 (.clk(clock_2_out), .D(in_5[0]), .Q(out_7[0]), .reset(clear_2));  // open: Qn, preset, en
  D_Flip_Flop d_ff_10 (.clk(clock_2_out), .D(in_5[1]), .Q(out_7[1]), .reset(clear_2));  // open: Qn, preset, en
  D_Flip_Flop d_ff_11 (.clk(clock_2_out), .D(in_5[2]), .Q(out_7[2]), .reset(clear_2));  // open: Qn, preset, en
  D_Flip_Flop d_ff_12 (.clk(clock_2_out), .D(in_5[3]), .Q(out_7[3]), .reset(clear_2));  // open: Qn, preset, en
  D_Flip_Flop d_ff_13 (.clk(clock_2_out), .D(in_5[4]), .Q(out_7[4]), .reset(clear_2));  // open: Qn, preset, en
  D_Flip_Flop d_ff_14 (.clk(clock_2_out), .D(in_5[5]), .Q(out_7[5]), .reset(clear_2));  // open: Qn, preset, en
  D_Flip_Flop d_ff_15 (.clk(clock_2_out), .D(in_5[6]), .Q(out_7[6]), .reset(clear_2));  // open: Qn, preset, en
  D_Flip_Flop d_ff_16 (.clk(clock_2_out), .D(in_5[7]), .Q(out_7[7]), .reset(clear_2));  // open: Qn, preset, en

  // Notes on the sheet:
  //   input
  //   forward
  //   input
  //   output
  //   синхронный режим
  //   output
  //   асинхронный режим
endmodule

module \память_8_бит  (
  input  [7:0] in_1,
  input  \выполнить ,
  input  clean,
  input  in_4,
  input  in_5,
  input  \выбрать_канал ,
  output [7:0] \output 
);

  wire clock_1_out, demultiplexer_1_out0, demultiplexer_1_out1, demultiplexer_1_out2, demultiplexer_1_out3,
       demultiplexer_1_out4, demultiplexer_1_out5, demultiplexer_1_out6, demultiplexer_1_out7;
  wire [7:0] register_1_q, register_2_q, register_3_q, register_4_q, register_5_q, register_6_q,
       register_7_q, register_8_q;

  Demultiplexer #(.select(3)) demultiplexer_1 (
    .out0(demultiplexer_1_out0), .out1(demultiplexer_1_out1), .out2(demultiplexer_1_out2),
    .out3(demultiplexer_1_out3), .out4(demultiplexer_1_out4), .out5(demultiplexer_1_out5),
    .out6(demultiplexer_1_out6), .out7(demultiplexer_1_out7), .in(\выполнить ),
    .sel({\выбрать_канал , in_5, in_4}));  // open: en
  Clock clock_1 (.out(clock_1_out));
  Register register_1 (.D(in_1), .en(demultiplexer_1_out0), .Q(register_1_q), .clk(clock_1_out), .clr(clean));
  Register register_2 (.D(in_1), .en(demultiplexer_1_out1), .Q(register_2_q), .clk(clock_1_out), .clr(clean));
  Register register_3 (.D(in_1), .en(demultiplexer_1_out2), .Q(register_3_q), .clk(clock_1_out), .clr(clean));
  Register register_4 (.D(in_1), .en(demultiplexer_1_out3), .Q(register_4_q), .clk(clock_1_out), .clr(clean));
  Register register_5 (.D(in_1), .en(demultiplexer_1_out4), .Q(register_5_q), .clk(clock_1_out), .clr(clean));
  Register register_6 (.D(in_1), .en(demultiplexer_1_out5), .Q(register_6_q), .clk(clock_1_out), .clr(clean));
  Register register_7 (.D(in_1), .en(demultiplexer_1_out6), .Q(register_7_q), .clk(clock_1_out), .clr(clean));
  Register register_8 (.D(in_1), .en(demultiplexer_1_out7), .Q(register_8_q), .clk(clock_1_out), .clr(clean));
  Multiplexer #(.select(3), .width(8)) multiplexer_1 (
    .in0(register_1_q), .in1(register_2_q), .in2(register_3_q), .in3(register_4_q), .in4(register_5_q),
    .in5(register_6_q), .in6(register_7_q), .in7(register_8_q), .out(\output ),
    .sel({\выбрать_канал , in_5, in_4}));  // open: en

  // Notes on the sheet:
  //   input
endmodule

module _16_1 (
  input  [7:0] in_1,
  input  in_2,
  input  in_3,
  input  in_4,
  input  in_5,
  input  in_6,
  input  in_7,
  output [7:0] out_8
);

  wire [7:0] demultiplexer_1_out0, demultiplexer_1_out1, \память_8_бит_1_output , \память_8_бит_2_output ;

  \память_8_бит  \u_память_8_бит_1  (
    .in_1(demultiplexer_1_out0), .\выполнить (in_6), .in_4(in_3), .in_5(in_4), .\выбрать_канал (in_5),
    .\output (\память_8_бит_1_output ));  // open: clean
  Demultiplexer #(.width(8)) demultiplexer_1 (
    .out0(demultiplexer_1_out0), .out1(demultiplexer_1_out1), .in(in_1), .sel(in_2));  // open: en
  Multiplexer #(.width(8)) multiplexer_1 (
    .in0(\память_8_бит_1_output ), .in1(\память_8_бит_2_output ), .out(out_8), .sel(in_2));  // open: en
  \память_8_бит  \u_память_8_бит_2  (
    .in_1(demultiplexer_1_out1), .\выполнить (in_6), .in_4(in_3), .in_5(in_4), .\выбрать_канал (in_5),
    .\output (\память_8_бит_2_output ));  // open: clean
endmodule

module _32_2 (
  input  [7:0] in_1,
  input  in_2,
  input  in_3,
  input  in_4,
  input  in_5,
  input  in_6,
  input  in_7,
  input  in_8,
  output [7:0] out_9
);

  wire [7:0] demultiplexer_1_out0, demultiplexer_1_out1, n16_1_1_out_8, n16_1_2_out_8;

  _16_1 u_16_1_1 (
    .in_6(in_7), .in_7(in_8), .in_3(in_3), .in_4(in_4), .in_5(in_5), .in_1(demultiplexer_1_out0),
    .in_2(in_6), .out_8(n16_1_1_out_8));
  Demultiplexer #(.width(8)) demultiplexer_1 (
    .out0(demultiplexer_1_out0), .out1(demultiplexer_1_out1), .in(in_1), .sel(in_2));  // open: en
  Multiplexer #(.width(8)) multiplexer_1 (
    .in0(n16_1_1_out_8), .in1(n16_1_2_out_8), .out(out_9), .sel(in_2));  // open: en
  _16_1 u_16_1_2 (
    .in_6(in_7), .in_7(in_8), .in_3(in_3), .in_4(in_4), .in_5(in_5), .in_1(demultiplexer_1_out1),
    .in_2(in_6), .out_8(n16_1_2_out_8));
endmodule

module _64_3 (
  input  [7:0] in_1,
  input  in_2,
  input  in_3,
  input  in_4,
  input  in_5,
  input  in_6,
  input  in_7,
  input  in_8,
  input  in_9,
  output [7:0] out_10
);

  wire [7:0] demultiplexer_1_out0, demultiplexer_1_out1, n32_2_1_out_9, n32_2_2_out_9;

  _32_2 u_32_2_1 (
    .in_7(in_8), .in_8(in_9), .in_3(in_3), .in_4(in_4), .in_5(in_5), .in_6(in_6),
    .in_1(demultiplexer_1_out0), .in_2(in_7), .out_9(n32_2_1_out_9));
  Demultiplexer #(.width(8)) demultiplexer_1 (
    .out0(demultiplexer_1_out0), .out1(demultiplexer_1_out1), .in(in_1), .sel(in_2));  // open: en
  Multiplexer #(.width(8)) multiplexer_1 (
    .in0(n32_2_1_out_9), .in1(n32_2_2_out_9), .out(out_10), .sel(in_2));  // open: en
  _32_2 u_32_2_2 (
    .in_7(in_8), .in_8(in_9), .in_3(in_3), .in_4(in_4), .in_5(in_5), .in_6(in_6),
    .in_1(demultiplexer_1_out1), .in_2(in_7), .out_9(n32_2_2_out_9));
endmodule

module _128_4 (
  input  in_1,
  input  [7:0] in_2,
  input  in_3,
  input  in_4,
  input  in_5,
  input  in_6,
  input  in_7,
  input  in_8,
  input  in_9,
  input  in_10,
  output [7:0] out_11
);

  wire [7:0] demultiplexer_1_out0, demultiplexer_1_out1, n64_3_1_out_10, n64_3_2_out_10;

  _64_3 u_64_3_1 (
    .in_8(in_9), .in_9(in_10), .in_3(in_3), .in_4(in_4), .in_5(in_5), .in_6(in_6), .in_7(in_7),
    .in_1(demultiplexer_1_out0), .in_2(in_8), .out_10(n64_3_1_out_10));
  Multiplexer #(.width(8)) multiplexer_1 (
    .in0(n64_3_1_out_10), .in1(n64_3_2_out_10), .out(out_11), .sel(in_1));  // open: en
  Demultiplexer #(.width(8)) demultiplexer_1 (
    .out0(demultiplexer_1_out0), .out1(demultiplexer_1_out1), .in(in_2), .sel(in_1));  // open: en
  _64_3 u_64_3_2 (
    .in_8(in_9), .in_9(in_10), .in_3(in_3), .in_4(in_4), .in_5(in_5), .in_6(in_6), .in_7(in_7),
    .in_1(demultiplexer_1_out1), .in_2(in_8), .out_10(n64_3_2_out_10));
endmodule

module _256_5 (
  input  [7:0] in_1,
  input  in_2,
  input  in_3,
  input  in_4,
  input  in_5,
  input  in_6,
  input  in_7,
  input  in_8,
  input  in_9,
  input  in_10,
  input  in_11,
  output [7:0] out_12
);

  wire [7:0] demultiplexer_1_out0, demultiplexer_1_out1, n128_4_1_out_11, n128_4_2_out_11;

  _128_4 u_128_4_1 (
    .in_9(in_10), .in_1(in_9), .in_10(in_11), .in_3(in_3), .in_4(in_4), .in_5(in_5), .in_6(in_6),
    .in_7(in_7), .in_8(in_8), .in_2(demultiplexer_1_out0), .out_11(n128_4_1_out_11));
  Demultiplexer #(.width(8)) demultiplexer_1 (
    .out0(demultiplexer_1_out0), .out1(demultiplexer_1_out1), .in(in_1), .sel(in_2));  // open: en
  Multiplexer #(.width(8)) multiplexer_1 (
    .in0(n128_4_1_out_11), .in1(n128_4_2_out_11), .out(out_12), .sel(in_2));  // open: en
  _128_4 u_128_4_2 (
    .in_9(in_10), .in_1(in_9), .in_10(in_11), .in_3(in_3), .in_4(in_4), .in_5(in_5), .in_6(in_6),
    .in_7(in_7), .in_8(in_8), .in_2(demultiplexer_1_out1), .out_11(n128_4_2_out_11));
endmodule

module _512_6 (
  input  [7:0] in_1,
  input  in_2,
  input  in_3,
  input  in_4,
  input  in_5,
  input  in_6,
  input  in_7,
  input  in_8,
  input  in_9,
  input  in_10,
  input  in_11,
  input  in_12,
  output [7:0] out_13
);

  wire [7:0] demultiplexer_1_out0, demultiplexer_1_out1, n256_5_1_out_12, n256_5_2_out_12;

  _256_5 u_256_5_1 (
    .in_10(in_11), .in_2(in_10), .in_11(in_12), .in_3(in_3), .in_4(in_4), .in_5(in_5), .in_6(in_6),
    .in_7(in_7), .in_8(in_8), .in_9(in_9), .in_1(demultiplexer_1_out0), .out_12(n256_5_1_out_12));
  Multiplexer #(.width(8)) multiplexer_1 (
    .in0(n256_5_1_out_12), .in1(n256_5_2_out_12), .out(out_13), .sel(in_2));  // open: en
  Demultiplexer #(.width(8)) demultiplexer_1 (
    .out0(demultiplexer_1_out0), .out1(demultiplexer_1_out1), .in(in_1), .sel(in_2));  // open: en
  _256_5 u_256_5_2 (
    .in_10(in_11), .in_2(in_10), .in_11(in_12), .in_3(in_3), .in_4(in_4), .in_5(in_5), .in_6(in_6),
    .in_7(in_7), .in_8(in_8), .in_9(in_9), .in_1(demultiplexer_1_out1), .out_12(n256_5_2_out_12));
endmodule

module _1024_7 (
  input  [7:0] in_1,
  input  in_2,
  input  in_3,
  input  in_4,
  input  in_5,
  input  in_6,
  input  in_7,
  input  in_8,
  input  in_9,
  input  in_10,
  input  in_11,
  input  in_12,
  input  in_13,
  output [7:0] out_14
);

  wire [7:0] demultiplexer_1_out0, demultiplexer_1_out1, n512_6_1_out_13, n512_6_2_out_13;

  _512_6 u_512_6_1 (
    .in_11(in_12), .in_2(in_10), .in_12(in_13), .in_3(in_2), .in_4(in_3), .in_5(in_4), .in_6(in_5),
    .in_7(in_6), .in_8(in_7), .in_9(in_8), .in_10(in_9), .in_1(demultiplexer_1_out0), .out_13(n512_6_1_out_13));
  Demultiplexer #(.width(8)) demultiplexer_1 (
    .out0(demultiplexer_1_out0), .out1(demultiplexer_1_out1), .in(in_1), .sel(in_11));  // open: en
  Multiplexer #(.width(8)) multiplexer_1 (
    .in0(n512_6_1_out_13), .in1(n512_6_2_out_13), .out(out_14), .sel(in_11));  // open: en
  _512_6 u_512_6_2 (
    .in_11(in_12), .in_2(in_10), .in_12(in_13), .in_3(in_2), .in_4(in_3), .in_5(in_4), .in_6(in_5),
    .in_7(in_6), .in_8(in_7), .in_9(in_8), .in_10(in_9), .in_1(demultiplexer_1_out1), .out_13(n512_6_2_out_13));
endmodule

module \память_1024_бит  (
  input  [9:0] in_1,
  input  [7:0] in_2,
  input  \запуск ,
  output [7:0] out_4
);

  wire clock_1_out;

  Clock clock_1 (.out(clock_1_out));
  _1024_7 u_1024_7_1 (
    .in_11(in_1[9]), .in_12(\запуск ), .in_13(clock_1_out), .in_2(in_1[0]), .in_3(in_1[1]), .in_4(in_1[2]),
    .in_5(in_1[3]), .in_6(in_1[4]), .in_7(in_1[5]), .in_8(in_1[6]), .in_9(in_1[7]), .in_10(in_1[8]),
    .in_1(in_2), .out_14(out_4));

  // Notes on the sheet:
  //   выбор каналов
  //   input
  //   generation
  //   output
endmodule

module \jk_триггер  (
  input  K,
  input  J,
  output output_2,
  output output_1
);

  wire and_1_out, and_2_out, clock_1_out;

  Clock clock_1 (.out(clock_1_out));
  and and_1 (and_1_out, output_2, K, clock_1_out);
  and and_2 (and_2_out, clock_1_out, J, output_1);
  nor nor_1 (output_2, and_1_out, output_1);
  nor nor_2 (output_1, output_2, and_2_out);
endmodule
