// Logisim project лабараторнаяЧипчиковБПИ2306.circ as structural Verilog: 11 circuits, main circuit шифр 10-2
module \шифр_10_2  (
  input  x9,
  input  x8,
  input  x7,
  input  x6,
  input  x5,
  input  x4,
  input  x3,
  input  x2,
  input  x1,
  input  x0,
  output ERROR,
  output y3,
  output y2,
  output y1,
  output y0
);

  wire and_1_out, and_2_out, and_3_out, and_4_out, and_5_out, and_6_out, and_7_out, and_8_out, and_9_out,
       and_10_out, and_11_out, and_12_out, and_13_out, and_14_out, and_15_out, and_16_out, and_17_out,
       and_18_out, and_19_out, and_20_out, and_21_out, and_22_out, and_23_out, and_24_out, and_25_out,
       and_26_out, and_27_out, and_28_out, and_29_out, and_30_out, and_31_out, and_32_out, and_33_out,
       and_34_out, and_35_out, and_36_out, and_37_out, and_38_out, and_39_out, and_40_out, and_41_out,
       and_42_out, and_43_out, and_44_out, and_45_out, and_46_out, and_47_out, and_48_out, and_49_out,
       and_50_out, and_51_out, and_52_out, and_53_out, and_54_out, and_55_out, and_56_out, and_57_out,
       and_58_out, and_59_out, and_60_out, and_61_out, and_62_out, and_63_out, not_1_out, not_2_out,
       not_3_out, not_4_out, not_5_out, not_6_out, not_7_out, not_8_out, not_9_out, not_10_out, not_11_out,
       not_12_out, not_13_out, not_14_out, not_15_out, not_16_out, not_17_out, not_18_out, not_19_out,
       not_20_out, not_21_out, not_22_out, not_23_out, not_24_out, not_25_out, not_26_out, not_27_out,
       not_28_out, not_29_out, not_30_out, not_31_out, not_32_out, not_33_out, not_34_out, not_35_out,
       not_36_out, not_37_out, not_38_out, not_39_out, not_40_out, not_41_out, not_42_out, not_43_out,
       not_44_out, not_45_out, not_46_out, not_47_out, not_48_out, not_49_out, not_50_out, not_51_out,
       not_52_out, not_53_out, not_54_out, not_55_out, not_56_out, not_57_out, not_58_out, not_59_out,
       not_60_out, not_61_out, not_62_out, not_63_out, not_64_out, not_65_out, not_66_out, not_67_out,
       not_68_out, not_69_out, not_70_out, not_71_out, not_72_out, not_73_out, not_74_out, not_75_out,
       not_76_out, not_77_out, not_78_out, not_79_out, not_80_out, not_81_out, not_82_out, not_83_out,
       not_84_out, not_85_out, not_86_out, not_87_out, not_88_out, not_89_out, not_90_out, not_91_out,
       not_92_out, not_93_out, not_94_out, not_95_out, not_96_out, not_97_out, not_98_out, not_99_out,
       not_100_out, not_101_out, not_102_out, not_103_out, not_104_out, not_105_out, not_106_out,
       not_107_out, not_108_out, not_109_out, not_110_out, not_111_out, not_112_out, not_113_out,
       not_114_out, not_115_out, not_116_out, not_117_out, not_118_out, not_119_out, not_120_out,
       not_121_out, not_122_out, not_123_out, not_124_out, not_125_out, not_126_out, not_127_out,
       not_128_out, not_129_out, not_130_out, not_131_out, not_132_out, not_133_out, not_134_out,
       not_135_out, not_136_out, not_137_out, not_138_out, not_139_out, not_140_out, not_141_out,
       not_142_out, not_143_out, not_144_out, not_145_out, not_146_out, not_147_out, not_148_out,
       not_149_out, not_150_out, not_151_out, not_152_out, not_153_out, not_154_out, not_155_out,
       not_156_out, not_157_out, not_158_out, not_159_out, not_160_out, not_161_out, not_162_out,
       not_163_out, not_164_out, not_165_out, not_166_out, not_167_out, not_168_out, not_169_out,
       not_170_out, not_171_out, not_172_out, not_173_out, not_174_out, not_175_out, or_5_out, or_7_out;

  not not_1 (not_1_out, x9);
  not not_2 (not_2_out, x8);
  not not_3 (not_3_out, x6);
  not not_4 (not_4_out, x5);
  not not_5 (not_5_out, x4);
  not not_6 (not_6_out, x3);
  not not_7 (not_7_out, x2);
  not not_8 (not_8_out, x1);
  not not_9 (not_9_out, x0);
  not not_10 (not_10_out, x9);
  not not_11 (not_11_out, x7);
  not not_12 (not_12_out, x6);
  not not_13 (not_13_out, x5);
  not not_14 (not_14_out, x4);
  not not_15 (not_15_out, x3);
  not not_16 (not_16_out, x2);
  not not_17 (not_17_out, x1);
  not not_18 (not_18_out, x0);
  not not_19 (not_19_out, x8);
  not not_20 (not_20_out, x7);
  not not_21 (not_21_out, x6);
  not not_22 (not_22_out, x5);
  not not_23 (not_23_out, x4);
  not not_24 (not_24_out, x3);
  not not_25 (not_25_out, x2);
  not not_26 (not_26_out, x1);
  not not_27 (not_27_out, x0);
  not not_28 (not_28_out, x9);
  not not_29 (not_29_out, x8);
  not not_30 (not_30_out, x7);
  not not_31 (not_31_out, x6);
  not not_32 (not_32_out, x5);
  not not_33 (not_33_out, x3);
  not not_34 (not_34_out, x2);
  not not_35 (not_35_out, x1);
  not not_36 (not_36_out, x0);
  not not_37 (not_37_out, x9);
  not not_38 (not_38_out, x8);
  not not_39 (not_39_out, x7);
  not not_40 (not_40_out, x6);
  not not_41 (not_41_out, x4);
  not not_42 (not_42_out, x3);
  not not_43 (not_43_out, x2);
  not not_44 (not_44_out, x1);
  not not_45 (not_45_out, x0);
  not not_46 (not_46_out, x9);
  not not_47 (not_47_out, x8);
  not not_48 (not_48_out, x7);
  not not_49 (not_49_out, x5);
  not not_50 (not_50_out, x4);
  not not_51 (not_51_out, x3);
  not not_52 (not_52_out, x2);
  not not_53 (not_53_out, x1);
  not not_54 (not_54_out, x0);
  not not_55 (not_55_out, x9);
  not not_56 (not_56_out, x8);
  not not_57 (not_57_out, x6);
  not not_58 (not_58_out, x5);
  not not_59 (not_59_out, x4);
  not not_60 (not_60_out, x3);
  not not_61 (not_61_out, x2);
  not not_62 (not_62_out, x1);
  not not_63 (not_63_out, x0);
  not not_64 (not_64_out, x9);
  not not_65 (not_65_out, x8);
  not not_66 (not_66_out, x7);
  not not_67 (not_67_out, x6);
  not not_68 (not_68_out, x5);
  not not_69 (not_69_out, x4);
  not not_70 (not_70_out, x3);
  not not_71 (not_71_out, x1);
  not not_72 (not_72_out, x0);
  not not_73 (not_73_out, x9);
  not not_74 (not_74_out, x8);
  not not_75 (not_75_out, x7);
  not not_76 (not_76_out, x6);
  not not_77 (not_77_out, x5);
  not not_78 (not_78_out, x4);
  not not_79 (not_79_out, x2);
  not not_80 (not_80_out, x1);
  not not_81 (not_81_out, x0);
  not not_82 (not_82_out, x9);
  not not_83 (not_83_out, x8);
  not not_84 (not_84_out, x7);
  not not_85 (not_85_out, x5);
  not not_86 (not_86_out, x4);
  not not_87 (not_87_out, x3);
  not not_88 (not_88_out, x2);
  not not_89 (not_89_out, x1);
  not not_90 (not_90_out, x0);
  not not_91 (not_91_out, x9);
  not not_92 (not_92_out, x8);
  not not_93 (not_93_out, x6);
  not not_94 (not_94_out, x5);
  not not_95 (not_95_out, x4);
  not not_96 (not_96_out, x3);
  not not_97 (not_97_out, x2);
  not not_98 (not_98_out, x1);
  not not_99 (not_99_out, x0);
  not not_100 (not_100_out, x9);
  not not_101 (not_101_out, x7);
  not not_102 (not_102_out, x4);
  not not_103 (not_103_out, x3);
  not not_104 (not_104_out, x1);
  not not_105 (not_105_out, x0);
  not not_106 (not_106_out, x9);
  not not_107 (not_107_out, x8);
  not not_108 (not_108_out, x7);
  not not_109 (not_109_out, x6);
  not not_110 (not_110_out, x4);
  not not_111 (not_111_out, x3);
  not not_112 (not_112_out, x2);
  not not_113 (not_113_out, x0);
  not not_114 (not_114_out, x9);
  not not_115 (not_115_out, x8);
  not not_116 (not_116_out, x7);
  not not_117 (not_117_out, x6);
  not not_118 (not_118_out, x5);
  not not_119 (not_119_out, x4);
  not not_120 (not_120_out, x2);
  not not_121 (not_121_out, x1);
  not not_122 (not_122_out, x0);
  not not_123 (not_123_out, x9);
  not not_124 (not_124_out, x8);
  not not_125 (not_125_out, x7);
  not not_126 (not_126_out, x6);
  not not_127 (not_127_out, x4);
  not not_128 (not_128_out, x3);
  not not_129 (not_129_out, x2);
  not not_130 (not_130_out, x0);
  not not_131 (not_131_out, x9);
  not not_132 (not_132_out, x8);
  not not_133 (not_133_out, x6);
  not not_134 (not_134_out, x5);
  not not_135 (not_135_out, x4);
  not not_136 (not_136_out, x3);
  not not_137 (not_137_out, x2);
  not not_138 (not_138_out, x1);
  not not_139 (not_139_out, x0);
  not not_140 (not_140_out, x9);
  not not_141 (not_141_out, x7);
  not not_142 (not_142_out, x6);
  not not_143 (not_143_out, x3);
  not not_144 (not_144_out, x2);
  not not_145 (not_145_out, x0);
  not not_146 (not_146_out, x8);
  not not_147 (not_147_out, x7);
  not not_148 (not_148_out, x6);
  not not_149 (not_149_out, x5);
  not not_150 (not_150_out, x4);
  not not_151 (not_151_out, x3);
  not not_152 (not_152_out, x2);
  not not_153 (not_153_out, x1);
  not not_154 (not_154_out, x0);
  not not_155 (not_155_out, x9);
  not not_156 (not_156_out, x8);
  not not_157 (not_157_out, x7);
  not not_158 (not_158_out, x6);
  not not_159 (not_159_out, x5);
  not not_160 (not_160_out, x4);
  not not_161 (not_161_out, x3);
  not not_162 (not_162_out, x2);
  not not_163 (not_163_out, x1);
  not not_164 (not_164_out, x0);
  not not_165 (not_165_out, x6);
  not not_166 (not_166_out, x4);
  and and_1 (and_1_out, not_1_out, not_2_out, x7, not_3_out, not_4_out, not_5_out, not_6_out, not_7_out, not_8_out, not_9_out);
  and and_2 (and_2_out, not_10_out, x8, not_11_out, not_12_out, not_13_out, not_14_out, not_15_out, not_16_out, not_17_out, not_18_out);
  and and_3 (and_3_out, x9, not_19_out, not_20_out, not_21_out, not_22_out, not_23_out, not_24_out, not_25_out, not_26_out, not_27_out);
  and and_4 (and_4_out, not_28_out, not_29_out, not_30_out, not_31_out, not_32_out, x4, not_33_out, not_34_out, not_35_out, not_36_out);
  and and_5 (and_5_out, not_37_out, not_38_out, not_39_out, not_40_out, x5, not_41_out, not_42_out, not_43_out, not_44_out, not_45_out);
  and and_6 (and_6_out, not_46_out, not_47_out, not_48_out, x6, not_49_out, not_50_out, not_51_out, not_52_out, not_53_out, not_54_out);
  and and_7 (and_7_out, not_55_out, not_56_out, x7, not_57_out, not_58_out, not_59_out, not_60_out, not_61_out, not_62_out, not_63_out);
  and and_8 (and_8_out, not_64_out, not_65_out, not_66_out, not_67_out, not_68_out, not_69_out, not_70_out, x2, not_71_out, not_72_out);
  and and_9 (and_9_out, not_73_out, not_74_out, not_75_out, not_76_out, not_77_out, not_78_out, x3, not_79_out, not_80_out, not_81_out);
  and and_10 (and_10_out, not_82_out, not_83_out, not_84_out, x6, not_85_out, not_86_out, not_87_out, not_88_out, not_89_out, not_90_out);
  and and_11 (and_11_out, not_91_out, not_92_out, x7, not_93_out, not_94_out, not_95_out, not_96_out, not_97_out, not_98_out, not_99_out);
  and and_12 (and_12_out, not_100_out, x8, not_101_out, x6, x5, not_102_out, not_103_out, x2, not_104_out, not_105_out);
  and and_13 (and_13_out, not_106_out, not_107_out, not_108_out, not_109_out, not_110_out, not_111_out, not_112_out, x1, not_113_out);
  and and_14 (and_14_out, not_114_out, not_115_out, not_116_out, not_117_out, not_118_out, not_119_out, x3, not_120_out, not_121_out, not_122_out);
  and and_15 (and_15_out, not_123_out, not_124_out, not_125_out, not_126_out, x5, not_127_out, not_128_out, not_129_out, not_130_out);
  and and_16 (and_16_out, not_131_out, not_132_out, x7, not_133_out, not_134_out, not_135_out, not_136_out, not_137_out, not_138_out, not_139_out);
  and and_17 (and_17_out, not_140_out, x8, not_141_out, not_142_out, x5, x4, not_143_out, not_144_out, x1, not_145_out);
  and and_18 (and_18_out, x9, not_146_out, not_147_out, not_148_out, not_149_out, not_150_out, not_151_out, not_152_out, not_153_out, not_154_out);
  and and_19 (and_19_out, not_155_out, not_156_out, not_157_out, not_158_out, not_159_out, not_160_out, not_161_out, not_162_out, not_163_out, not_164_out);
  and and_20 (and_20_out, x1, x0);
  and and_21 (and_21_out, x2, x0);
  and and_22 (and_22_out, x2, x1);
  and and_23 (and_23_out, x3, x0);
  and and_24 (and_24_out, x3, x1);
  and and_25 (and_25_out, x3, x2);
  and and_26 (and_26_out, x4, x0);
  not not_167 (not_167_out, x5);
  and and_27 (and_27_out, not_167_out, x4, x1);
  and and_28 (and_28_out, x4, x2);
  and and_29 (and_29_out, x4, x3);
  and and_30 (and_30_out, x5, x0);
  not not_168 (not_168_out, x8);
  and and_31 (and_31_out, not_168_out, x5, x1);
  not not_169 (not_169_out, x6);
  and and_32 (and_32_out, not_169_out, x5, x2);
  and and_33 (and_33_out, x5, x3);
  and and_34 (and_34_out, x5, x4, not_170_out);
  not not_170 (not_170_out, x1);
  and and_35 (and_35_out, x6, x0);
  and and_36 (and_36_out, x6, x1);
  and and_37 (and_37_out, x6, x3);
  and and_38 (and_38_out, x6, x4);
  not not_171 (not_171_out, x8);
  and and_39 (and_39_out, not_171_out, x6, x5);
  and and_40 (and_40_out, x7, x0);
  and and_41 (and_41_out, x7, x1);
  and and_42 (and_42_out, x7, x2);
  and and_43 (and_43_out, x7, x3);
  and and_44 (and_44_out, x7, x4);
  and and_45 (and_45_out, x7, x5);
  and and_46 (and_46_out, x7, x6);
  and and_47 (and_47_out, x8, x0);
  and and_48 (and_48_out, x8, not_172_out, x1);
  not not_172 (not_172_out, x5);
  and and_49 (and_49_out, x8, not_173_out, x2);
  not not_173 (not_173_out, x5);
  and and_50 (and_50_out, x8, x3);
  not not_174 (not_174_out, x5);
  and and_51 (and_51_out, x8, not_174_out, x4);
  and and_52 (and_52_out, x8, not_165_out, x5, not_166_out);
  and and_53 (and_53_out, x8, x6, not_175_out);
  not not_175 (not_175_out, x2);
  and and_54 (and_54_out, x8, x7);
  and and_55 (and_55_out, x9, x0);
  and and_56 (and_56_out, x9, x1);
  and and_57 (and_57_out, x9, x2);
  and and_58 (and_58_out, x9, x3);
  and and_59 (and_59_out, x9, x4);
  and and_60 (and_60_out, x9, x5);
  and and_61 (and_61_out, x9, x6);
  and and_62 (and_62_out, x9, x7);
  and and_63 (and_63_out, x9, x8);
  or or_1 (y3, and_1_out, and_2_out, and_3_out);
  or or_2 (y2, and_4_out, and_5_out, and_6_out, and_7_out);
  or or_3 (y1, and_8_out, and_9_out, and_10_out, and_11_out, and_12_out);
  or or_4 (y0, and_13_out, and_14_out, and_15_out, and_16_out, and_17_out, and_18_out);
  or or_5 (or_5_out, and_19_out, and_20_out, and_21_out, and_22_out, and_23_out, and_24_out, and_25_out, and_26_out, and_27_out, and_28_out, and_29_out, and_30_out, and_31_out, and_32_out, and_33_out, and_34_out, and_35_out, and_36_out, and_37_out, and_38_out, and_39_out, and_40_out, and_41_out);
  or or_6 (ERROR, or_5_out, or_7_out);
  or or_7 (or_7_out, and_42_out, and_43_out, and_44_out, and_45_out, and_46_out, and_47_out, and_48_out, and_49_out, and_50_out, and_51_out, and_52_out, and_53_out, and_54_out, and_55_out, and_56_out, and_57_out, and_58_out, and_59_out, and_60_out, and_61_out, and_62_out, and_63_out);
endmodule

module \дешифратор  (
  input  x9,
  input  x8,
  input  x7,
  input  x6,
  input  x5,
  input  x4,
  input  x3,
  input  x2,
  input  x1,
  input  x0,
  output y7,
  output y6,
  output y5,
  output y4,
  output y3,
  output y2,
  output y1,
  output y0,
  output ERROR
);

  wire and_2_out, and_3_out, and_4_out, and_5_out, and_6_out, and_7_out, and_8_out, and_9_out, and_10_out,
       and_11_out, and_12_out, and_13_out, and_14_out, and_15_out, and_16_out, and_17_out, and_18_out,
       and_19_out, and_20_out, and_21_out, and_22_out, and_23_out, and_24_out, and_25_out, and_26_out,
       and_27_out, and_28_out, and_29_out, and_30_out, and_31_out, and_32_out, and_33_out, and_34_out,
       and_35_out, and_36_out, and_37_out, and_38_out, and_39_out, and_40_out, and_41_out, and_42_out,
       and_43_out, and_44_out, and_45_out, and_46_out, and_47_out, and_48_out, and_49_out, and_50_out,
       and_51_out, and_52_out, and_53_out, and_54_out, and_55_out, and_56_out, and_57_out, and_58_out,
       and_59_out, and_60_out, and_61_out, and_62_out, and_63_out, and_64_out, and_65_out, and_66_out,
       and_67_out, and_68_out, and_69_out, and_70_out, and_71_out, and_72_out, and_73_out, and_74_out,
       and_75_out, and_76_out, and_77_out, and_78_out, and_79_out, and_80_out, and_81_out, and_82_out,
       and_83_out, and_84_out, and_85_out, and_86_out, and_87_out, and_88_out, and_89_out, and_90_out,
       and_91_out, and_92_out, and_93_out, and_94_out, and_95_out, and_96_out, not_1_out, not_2_out,
       not_3_out, not_4_out, not_5_out, not_6_out, not_7_out, not_8_out, not_9_out, not_10_out, not_11_out,
       not_12_out, not_13_out, not_14_out, not_15_out, not_16_out, not_17_out, not_18_out, not_19_out,
       not_20_out, not_21_out, not_22_out, not_23_out, not_24_out, not_25_out, not_26_out, not_27_out,
       not_28_out, not_29_out, not_30_out, not_31_out, not_32_out, not_33_out, not_34_out, not_35_out,
       not_36_out, not_37_out, not_38_out, not_39_out, not_40_out, not_41_out, not_42_out, not_43_out,
       not_44_out, not_45_out, not_46_out, not_47_out, not_48_out, not_49_out, not_50_out, not_51_out,
       not_52_out, not_53_out, not_54_out, not_55_out, not_56_out, not_57_out, not_58_out, not_59_out,
       not_60_out, not_61_out, not_62_out, not_63_out, not_64_out, not_65_out, not_66_out, not_67_out,
       not_68_out, not_69_out, not_70_out, not_71_out, not_72_out, not_73_out, not_74_out, not_75_out,
       not_76_out, not_77_out, not_78_out, not_79_out, not_80_out, not_81_out, not_82_out, not_83_out,
       not_84_out, not_85_out, not_86_out, not_87_out, not_88_out, not_89_out, not_90_out, not_91_out,
       not_92_out, not_93_out, not_94_out, not_95_out, not_96_out, not_97_out, not_98_out, not_99_out,
       not_100_out, not_101_out, not_102_out, not_103_out, not_104_out, not_105_out, not_106_out,
       not_107_out, not_108_out, not_109_out, not_110_out, not_111_out, not_112_out, not_113_out,
       not_114_out, not_115_out, not_116_out, not_117_out, not_118_out, not_119_out, not_120_out,
       not_121_out, not_122_out, not_123_out, not_124_out, not_125_out, not_126_out, not_127_out,
       not_128_out, not_129_out, not_130_out, not_131_out, not_132_out, not_133_out, not_134_out,
       not_135_out, not_136_out, not_137_out, not_138_out, not_139_out, not_140_out, not_141_out,
       not_142_out, not_143_out, not_144_out, not_145_out, not_146_out, not_147_out, not_148_out,
       not_149_out, not_150_out, not_151_out, not_152_out, not_153_out, not_154_out, not_155_out,
       not_156_out, not_157_out, not_158_out, not_159_out, not_160_out, not_161_out, not_162_out,
       not_163_out, not_164_out, not_165_out, not_166_out, not_167_out, not_168_out, not_169_out,
       not_170_out, not_171_out, not_172_out, not_173_out, not_174_out, not_175_out, not_176_out,
       not_177_out, not_178_out, not_179_out, not_180_out, not_181_out, not_182_out, not_183_out,
       not_184_out, not_185_out, not_186_out, not_187_out, not_188_out, not_189_out, not_190_out,
       not_191_out, not_192_out, not_193_out, not_194_out, not_195_out, not_196_out, not_197_out,
       not_198_out, not_199_out, not_200_out, not_201_out, not_202_out, not_203_out, not_204_out,
       not_205_out, not_206_out, not_207_out, not_208_out, not_209_out, not_210_out, not_211_out,
       not_212_out, not_213_out, not_214_out, not_215_out, not_216_out, not_217_out, not_218_out,
       not_219_out, not_220_out, not_221_out, not_222_out, not_223_out, not_224_out, not_225_out,
       not_226_out, not_227_out, not_228_out, not_229_out, not_230_out, not_231_out, not_232_out,
       not_233_out, not_234_out, not_235_out, not_236_out, not_237_out, not_238_out, not_239_out,
       not_240_out, not_241_out, not_242_out, not_243_out, not_244_out, not_245_out, not_246_out,
       not_247_out, not_248_out, not_249_out, not_250_out, not_251_out, not_252_out, not_253_out,
       not_254_out, not_255_out, not_256_out, not_257_out, not_258_out, not_259_out, not_260_out,
       not_261_out, not_262_out, not_263_out, not_264_out, not_265_out, not_266_out, not_267_out,
       not_268_out, not_269_out, not_270_out, not_271_out, not_272_out, not_273_out, not_274_out,
       not_275_out, not_276_out, not_277_out, not_278_out, not_279_out, not_280_out, not_281_out,
       not_282_out, not_283_out, not_284_out, not_285_out, not_286_out, not_287_out, not_288_out,
       not_289_out, not_290_out, not_291_out, not_292_out, not_293_out, not_294_out, not_295_out,
       not_296_out, not_297_out, not_298_out, not_299_out, not_300_out, not_301_out, not_302_out,
       not_303_out, not_304_out, not_305_out, not_306_out, not_307_out, not_308_out, not_309_out,
       not_310_out, not_311_out, not_312_out, not_313_out, not_314_out, not_315_out, not_316_out,
       not_317_out, not_318_out, not_319_out, not_320_out, not_321_out, not_322_out, not_323_out,
       not_324_out, not_325_out, not_326_out, not_327_out, not_328_out, not_329_out, not_330_out,
       not_331_out, not_332_out, not_333_out, not_334_out, not_335_out, not_336_out, not_337_out,
       not_338_out, not_339_out, not_340_out, not_341_out, not_342_out, not_343_out, not_344_out,
       not_345_out, not_346_out, not_347_out, not_348_out, not_349_out, not_350_out, not_351_out,
       not_352_out, not_353_out, not_354_out, not_355_out, not_356_out, not_357_out, not_358_out,
       not_359_out, not_360_out, not_361_out, not_362_out, not_363_out, not_364_out, not_365_out,
       not_366_out, not_367_out, not_368_out, not_369_out, not_370_out, not_371_out, not_372_out,
       not_373_out, not_374_out, not_375_out, not_376_out, not_377_out, not_378_out, not_379_out,
       not_380_out, not_381_out, not_382_out, not_383_out, not_384_out, not_385_out, not_386_out,
       not_387_out, not_388_out, not_389_out, not_390_out, not_391_out, not_392_out, not_393_out,
       not_394_out, not_395_out, not_396_out, not_397_out, not_398_out, not_399_out, not_400_out,
       not_401_out, not_402_out, not_403_out, not_404_out, not_405_out, not_406_out, not_407_out,
       not_408_out, not_409_out, not_410_out, not_411_out, not_412_out, not_413_out, not_414_out,
       not_415_out, not_416_out, not_417_out, not_418_out, not_419_out, not_420_out, not_421_out,
       not_422_out, not_423_out, not_424_out, not_425_out, not_426_out, not_427_out, not_428_out,
       not_429_out, not_430_out, not_431_out, not_432_out, not_433_out, not_434_out, not_435_out,
       not_436_out, not_437_out, not_438_out, not_439_out, not_440_out, not_441_out, not_442_out,
       not_443_out, not_444_out, not_445_out, not_446_out, not_447_out, not_448_out, not_449_out,
       not_450_out, not_451_out, not_452_out, not_453_out, not_454_out, not_455_out, not_456_out,
       not_457_out, not_458_out, not_459_out, not_460_out, not_461_out, not_462_out, not_463_out,
       not_464_out, not_465_out, not_466_out, not_467_out, not_468_out, not_469_out, not_470_out,
       not_471_out, not_472_out, not_473_out, not_474_out, not_475_out, not_476_out, or_8_out, or_10_out;

  not not_1 (not_1_out, x9);
  not not_2 (not_2_out, x8);
  not not_3 (not_3_out, x7);
  not not_4 (not_4_out, x5);
  not not_5 (not_5_out, x4);
  not not_6 (not_6_out, x3);
  not not_7 (not_7_out, x2);
  not not_8 (not_8_out, x1);
  not not_9 (not_9_out, x0);
  not not_10 (not_10_out, x9);
  not not_11 (not_11_out, x8);
  not not_12 (not_12_out, x7);
  not not_13 (not_13_out, x6);
  not not_14 (not_14_out, x5);
  not not_15 (not_15_out, x4);
  not not_16 (not_16_out, x3);
  not not_17 (not_17_out, x2);
  not not_18 (not_18_out, x1);
  not not_19 (not_19_out, x9);
  not not_20 (not_20_out, x8);
  not not_21 (not_21_out, x7);
  not not_22 (not_22_out, x6);
  not not_23 (not_23_out, x5);
  not not_24 (not_24_out, x4);
  not not_25 (not_25_out, x3);
  not not_26 (not_26_out, x2);
  not not_27 (not_27_out, x0);
  not not_28 (not_28_out, x9);
  not not_29 (not_29_out, x8);
  not not_30 (not_30_out, x7);
  not not_31 (not_31_out, x6);
  not not_32 (not_32_out, x5);
  not not_33 (not_33_out, x4);
  not not_34 (not_34_out, x2);
  not not_35 (not_35_out, x1);
  not not_36 (not_36_out, x0);
  not not_37 (not_37_out, x9);
  not not_38 (not_38_out, x8);
  not not_39 (not_39_out, x7);
  not not_40 (not_40_out, x6);
  not not_41 (not_41_out, x5);
  not not_42 (not_42_out, x3);
  not not_43 (not_43_out, x2);
  not not_44 (not_44_out, x1);
  not not_45 (not_45_out, x0);
  not not_46 (not_46_out, x9);
  not not_47 (not_47_out, x8);
  not not_48 (not_48_out, x7);
  not not_49 (not_49_out, x6);
  not not_50 (not_50_out, x4);
  not not_51 (not_51_out, x3);
  not not_52 (not_52_out, x2);
  not not_53 (not_53_out, x1);
  not not_54 (not_54_out, x0);
  not not_55 (not_55_out, x9);
  not not_56 (not_56_out, x8);
  not not_57 (not_57_out, x7);
  not not_58 (not_58_out, x5);
  not not_59 (not_59_out, x4);
  not not_60 (not_60_out, x3);
  not not_61 (not_61_out, x2);
  not not_62 (not_62_out, x1);
  not not_63 (not_63_out, x0);
  not not_64 (not_64_out, x9);
  not not_65 (not_65_out, x8);
  not not_66 (not_66_out, x6);
  not not_67 (not_67_out, x5);
  not not_68 (not_68_out, x4);
  not not_69 (not_69_out, x3);
  not not_70 (not_70_out, x2);
  not not_71 (not_71_out, x1);
  not not_72 (not_72_out, x0);
  not not_73 (not_73_out, x9);
  not not_74 (not_74_out, x7);
  not not_75 (not_75_out, x6);
  not not_76 (not_76_out, x5);
  not not_77 (not_77_out, x4);
  not not_78 (not_78_out, x3);
  not not_79 (not_79_out, x2);
  not not_80 (not_80_out, x1);
  not not_81 (not_81_out, x0);
  not not_82 (not_82_out, x8);
  not not_83 (not_83_out, x7);
  not not_84 (not_84_out, x6);
  not not_85 (not_85_out, x5);
  not not_86 (not_86_out, x4);
  not not_87 (not_87_out, x3);
  not not_88 (not_88_out, x2);
  not not_89 (not_89_out, x1);
  not not_90 (not_90_out, x0);
  not not_91 (not_91_out, x9);
  not not_92 (not_92_out, x8);
  not not_93 (not_93_out, x7);
  not not_94 (not_94_out, x6);
  not not_95 (not_95_out, x5);
  not not_96 (not_96_out, x4);
  not not_97 (not_97_out, x3);
  not not_98 (not_98_out, x2);
  not not_99 (not_99_out, x1);
  not not_100 (not_100_out, x9);
  not not_101 (not_101_out, x8);
  not not_102 (not_102_out, x7);
  not not_103 (not_103_out, x6);
  not not_104 (not_104_out, x5);
  not not_105 (not_105_out, x4);
  not not_106 (not_106_out, x3);
  not not_107 (not_107_out, x1);
  not not_108 (not_108_out, x0);
  not not_109 (not_109_out, x9);
  not not_110 (not_110_out, x8);
  not not_111 (not_111_out, x7);
  not not_112 (not_112_out, x6);
  not not_113 (not_113_out, x5);
  not not_114 (not_114_out, x4);
  not not_115 (not_115_out, x2);
  not not_116 (not_116_out, x1);
  not not_117 (not_117_out, x0);
  not not_118 (not_118_out, x9);
  not not_119 (not_119_out, x8);
  not not_120 (not_120_out, x7);
  not not_121 (not_121_out, x6);
  not not_122 (not_122_out, x4);
  not not_123 (not_123_out, x3);
  not not_124 (not_124_out, x2);
  not not_125 (not_125_out, x1);
  not not_126 (not_126_out, x0);
  not not_127 (not_127_out, x9);
  not not_128 (not_128_out, x8);
  not not_129 (not_129_out, x7);
  not not_130 (not_130_out, x5);
  not not_131 (not_131_out, x4);
  not not_132 (not_132_out, x3);
  not not_133 (not_133_out, x2);
  not not_134 (not_134_out, x1);
  not not_135 (not_135_out, x0);
  not not_136 (not_136_out, x9);
  not not_137 (not_137_out, x7);
  not not_138 (not_138_out, x6);
  not not_139 (not_139_out, x5);
  not not_140 (not_140_out, x4);
  not not_141 (not_141_out, x3);
  not not_142 (not_142_out, x2);
  not not_143 (not_143_out, x1);
  not not_144 (not_144_out, x0);
  not not_145 (not_145_out, x8);
  not not_146 (not_146_out, x7);
  not not_147 (not_147_out, x6);
  not not_148 (not_148_out, x5);
  not not_149 (not_149_out, x4);
  not not_150 (not_150_out, x3);
  not not_151 (not_151_out, x2);
  not not_152 (not_152_out, x1);
  not not_153 (not_153_out, x0);
  not not_154 (not_154_out, x9);
  not not_155 (not_155_out, x8);
  not not_156 (not_156_out, x7);
  not not_157 (not_157_out, x6);
  not not_158 (not_158_out, x5);
  not not_159 (not_159_out, x4);
  not not_160 (not_160_out, x3);
  not not_161 (not_161_out, x2);
  not not_162 (not_162_out, x1);
  not not_163 (not_163_out, x9);
  not not_164 (not_164_out, x8);
  not not_165 (not_165_out, x7);
  not not_166 (not_166_out, x6);
  not not_167 (not_167_out, x5);
  not not_168 (not_168_out, x4);
  not not_169 (not_169_out, x3);
  not not_170 (not_170_out, x1);
  not not_171 (not_171_out, x0);
  not not_172 (not_172_out, x9);
  not not_173 (not_173_out, x8);
  not not_174 (not_174_out, x7);
  not not_175 (not_175_out, x5);
  not not_176 (not_176_out, x4);
  not not_177 (not_177_out, x3);
  not not_178 (not_178_out, x2);
  not not_179 (not_179_out, x1);
  not not_180 (not_180_out, x0);
  not not_181 (not_181_out, x9);
  not not_182 (not_182_out, x7);
  not not_183 (not_183_out, x6);
  not not_184 (not_184_out, x5);
  not not_185 (not_185_out, x4);
  not not_186 (not_186_out, x3);
  not not_187 (not_187_out, x2);
  not not_188 (not_188_out, x1);
  not not_189 (not_189_out, x0);
  not not_190 (not_190_out, x9);
  not not_191 (not_191_out, x8);
  not not_192 (not_192_out, x7);
  not not_193 (not_193_out, x6);
  not not_194 (not_194_out, x5);
  not not_195 (not_195_out, x4);
  not not_196 (not_196_out, x3);
  not not_197 (not_197_out, x1);
  not not_198 (not_198_out, x0);
  not not_199 (not_199_out, x9);
  not not_200 (not_200_out, x8);
  not not_201 (not_201_out, x7);
  not not_202 (not_202_out, x6);
  not not_203 (not_203_out, x5);
  not not_204 (not_204_out, x4);
  not not_205 (not_205_out, x2);
  not not_206 (not_206_out, x1);
  not not_207 (not_207_out, x0);
  not not_208 (not_208_out, x9);
  not not_209 (not_209_out, x8);
  not not_210 (not_210_out, x7);
  not not_211 (not_211_out, x6);
  not not_212 (not_212_out, x5);
  not not_213 (not_213_out, x3);
  not not_214 (not_214_out, x2);
  not not_215 (not_215_out, x1);
  not not_216 (not_216_out, x0);
  not not_217 (not_217_out, x9);
  not not_218 (not_218_out, x8);
  not not_219 (not_219_out, x7);
  not not_220 (not_220_out, x6);
  not not_221 (not_221_out, x4);
  not not_222 (not_222_out, x3);
  not not_223 (not_223_out, x2);
  not not_224 (not_224_out, x1);
  not not_225 (not_225_out, x0);
  not not_226 (not_226_out, x9);
  not not_227 (not_227_out, x8);
  not not_228 (not_228_out, x7);
  not not_229 (not_229_out, x5);
  not not_230 (not_230_out, x4);
  not not_231 (not_231_out, x3);
  not not_232 (not_232_out, x2);
  not not_233 (not_233_out, x1);
  not not_234 (not_234_out, x0);
  not not_235 (not_235_out, x9);
  not not_236 (not_236_out, x7);
  not not_237 (not_237_out, x6);
  not not_238 (not_238_out, x5);
  not not_239 (not_239_out, x4);
  not not_240 (not_240_out, x3);
  not not_241 (not_241_out, x2);
  not not_242 (not_242_out, x1);
  not not_243 (not_243_out, x0);
  not not_244 (not_244_out, x8);
  not not_245 (not_245_out, x7);
  not not_246 (not_246_out, x6);
  not not_247 (not_247_out, x5);
  not not_248 (not_248_out, x4);
  not not_249 (not_249_out, x3);
  not not_250 (not_250_out, x2);
  not not_251 (not_251_out, x1);
  not not_252 (not_252_out, x0);
  not not_253 (not_253_out, x9);
  not not_254 (not_254_out, x8);
  not not_255 (not_255_out, x7);
  not not_256 (not_256_out, x6);
  not not_257 (not_257_out, x5);
  not not_258 (not_258_out, x4);
  not not_259 (not_259_out, x3);
  not not_260 (not_260_out, x2);
  not not_261 (not_261_out, x1);
  not not_262 (not_262_out, x9);
  not not_263 (not_263_out, x8);
  not not_264 (not_264_out, x7);
  not not_265 (not_265_out, x6);
  not not_266 (not_266_out, x5);
  not not_267 (not_267_out, x3);
  not not_268 (not_268_out, x2);
  not not_269 (not_269_out, x1);
  not not_270 (not_270_out, x0);
  not not_271 (not_271_out, x9);
  not not_272 (not_272_out, x8);
  not not_273 (not_273_out, x7);
  not not_274 (not_274_out, x6);
  not not_275 (not_275_out, x4);
  not not_276 (not_276_out, x3);
  not not_277 (not_277_out, x2);
  not not_278 (not_278_out, x1);
  not not_279 (not_279_out, x0);
  not not_280 (not_280_out, x9);
  not not_281 (not_281_out, x8);
  not not_282 (not_282_out, x7);
  not not_283 (not_283_out, x5);
  not not_284 (not_284_out, x4);
  not not_285 (not_285_out, x3);
  not not_286 (not_286_out, x2);
  not not_287 (not_287_out, x1);
  not not_288 (not_288_out, x0);
  not not_289 (not_289_out, x9);
  not not_290 (not_290_out, x7);
  not not_291 (not_291_out, x6);
  not not_292 (not_292_out, x5);
  not not_293 (not_293_out, x4);
  not not_294 (not_294_out, x3);
  not not_295 (not_295_out, x2);
  not not_296 (not_296_out, x1);
  not not_297 (not_297_out, x0);
  not not_298 (not_298_out, x8);
  not not_299 (not_299_out, x7);
  not not_300 (not_300_out, x6);
  not not_301 (not_301_out, x5);
  not not_302 (not_302_out, x4);
  not not_303 (not_303_out, x3);
  not not_304 (not_304_out, x2);
  not not_305 (not_305_out, x1);
  not not_306 (not_306_out, x0);
  not not_307 (not_307_out, x9);
  not not_308 (not_308_out, x8);
  not not_309 (not_309_out, x7);
  not not_310 (not_310_out, x6);
  not not_311 (not_311_out, x5);
  not not_312 (not_312_out, x4);
  not not_313 (not_313_out, x3);
  not not_314 (not_314_out, x2);
  not not_315 (not_315_out, x1);
  not not_316 (not_316_out, x9);
  not not_317 (not_317_out, x8);
  not not_318 (not_318_out, x7);
  not not_319 (not_319_out, x6);
  not not_320 (not_320_out, x5);
  not not_321 (not_321_out, x4);
  not not_322 (not_322_out, x3);
  not not_323 (not_323_out, x1);
  not not_324 (not_324_out, x0);
  not not_325 (not_325_out, x9);
  not not_326 (not_326_out, x8);
  not not_327 (not_327_out, x7);
  not not_328 (not_328_out, x6);
  not not_329 (not_329_out, x5);
  not not_330 (not_330_out, x4);
  not not_331 (not_331_out, x2);
  not not_332 (not_332_out, x1);
  not not_333 (not_333_out, x0);
  not not_334 (not_334_out, x9);
  not not_335 (not_335_out, x8);
  not not_336 (not_336_out, x7);
  not not_337 (not_337_out, x6);
  not not_338 (not_338_out, x4);
  not not_339 (not_339_out, x3);
  not not_340 (not_340_out, x2);
  not not_341 (not_341_out, x1);
  not not_342 (not_342_out, x0);
  not not_343 (not_343_out, x9);
  not not_344 (not_344_out, x8);
  not not_345 (not_345_out, x7);
  not not_346 (not_346_out, x5);
  not not_347 (not_347_out, x4);
  not not_348 (not_348_out, x3);
  not not_349 (not_349_out, x2);
  not not_350 (not_350_out, x1);
  not not_351 (not_351_out, x0);
  not not_352 (not_352_out, x9);
  not not_353 (not_353_out, x8);
  not not_354 (not_354_out, x6);
  not not_355 (not_355_out, x5);
  not not_356 (not_356_out, x4);
  not not_357 (not_357_out, x3);
  not not_358 (not_358_out, x2);
  not not_359 (not_359_out, x1);
  not not_360 (not_360_out, x0);
  not not_361 (not_361_out, x9);
  not not_362 (not_362_out, x7);
  not not_363 (not_363_out, x6);
  not not_364 (not_364_out, x5);
  not not_365 (not_365_out, x4);
  not not_366 (not_366_out, x3);
  not not_367 (not_367_out, x2);
  not not_368 (not_368_out, x1);
  not not_369 (not_369_out, x0);
  not not_370 (not_370_out, x8);
  not not_371 (not_371_out, x7);
  not not_372 (not_372_out, x6);
  not not_373 (not_373_out, x5);
  not not_374 (not_374_out, x4);
  not not_375 (not_375_out, x3);
  not not_376 (not_376_out, x2);
  not not_377 (not_377_out, x1);
  not not_378 (not_378_out, x0);
  not not_379 (not_379_out, x9);
  not not_380 (not_380_out, x8);
  not not_381 (not_381_out, x7);
  not not_382 (not_382_out, x6);
  not not_383 (not_383_out, x5);
  not not_384 (not_384_out, x4);
  not not_385 (not_385_out, x3);
  not not_386 (not_386_out, x2);
  not not_387 (not_387_out, x1);
  not not_388 (not_388_out, x9);
  not not_389 (not_389_out, x8);
  not not_390 (not_390_out, x7);
  not not_391 (not_391_out, x6);
  not not_392 (not_392_out, x4);
  not not_393 (not_393_out, x3);
  not not_394 (not_394_out, x2);
  not not_395 (not_395_out, x0);
  not not_396 (not_396_out, x9);
  not not_397 (not_397_out, x8);
  not not_398 (not_398_out, x7);
  not not_399 (not_399_out, x6);
  not not_400 (not_400_out, x5);
  not not_401 (not_401_out, x4);
  not not_402 (not_402_out, x3);
  not not_403 (not_403_out, x1);
  not not_404 (not_404_out, x0);
  not not_405 (not_405_out, x9);
  not not_406 (not_406_out, x8);
  not not_407 (not_407_out, x7);
  not not_408 (not_408_out, x6);
  not not_409 (not_409_out, x5);
  not not_410 (not_410_out, x4);
  not not_411 (not_411_out, x2);
  not not_412 (not_412_out, x1);
  not not_413 (not_413_out, x0);
  not not_414 (not_414_out, x9);
  not not_415 (not_415_out, x8);
  not not_416 (not_416_out, x7);
  not not_417 (not_417_out, x6);
  not not_418 (not_418_out, x5);
  not not_419 (not_419_out, x3);
  not not_420 (not_420_out, x2);
  not not_421 (not_421_out, x1);
  not not_422 (not_422_out, x0);
  not not_423 (not_423_out, x9);
  not not_424 (not_424_out, x8);
  not not_425 (not_425_out, x6);
  not not_426 (not_426_out, x5);
  not not_427 (not_427_out, x4);
  not not_428 (not_428_out, x3);
  not not_429 (not_429_out, x2);
  not not_430 (not_430_out, x1);
  not not_431 (not_431_out, x0);
  not not_432 (not_432_out, x9);
  not not_433 (not_433_out, x7);
  not not_434 (not_434_out, x6);
  not not_435 (not_435_out, x5);
  not not_436 (not_436_out, x4);
  not not_437 (not_437_out, x3);
  not not_438 (not_438_out, x2);
  not not_439 (not_439_out, x1);
  not not_440 (not_440_out, x0);
  not not_441 (not_441_out, x9);
  not not_442 (not_442_out, x7);
  not not_443 (not_443_out, x6);
  not not_444 (not_444_out, x3);
  not not_445 (not_445_out, x2);
  not not_446 (not_446_out, x0);
  not not_447 (not_447_out, x8);
  not not_448 (not_448_out, x7);
  not not_449 (not_449_out, x6);
  not not_450 (not_450_out, x5);
  not not_451 (not_451_out, x4);
  not not_452 (not_452_out, x3);
  not not_453 (not_453_out, x2);
  not not_454 (not_454_out, x1);
  not not_455 (not_455_out, x0);
  not not_456 (not_456_out, x9);
  not not_457 (not_457_out, x8);
  not not_458 (not_458_out, x7);
  not not_459 (not_459_out, x6);
  not not_460 (not_460_out, x5);
  not not_461 (not_461_out, x4);
  not not_462 (not_462_out, x3);
  not not_463 (not_463_out, x2);
  not not_464 (not_464_out, x1);
  not not_465 (not_465_out, x0);
  not not_466 (not_466_out, x6);
  not not_467 (not_467_out, x4);
  and and_1 (y7, not_1_out, not_2_out, not_3_out, x6, not_4_out, not_5_out, not_6_out, not_7_out, not_8_out, not_9_out);
  and and_2 (and_2_out, not_10_out, not_11_out, not_12_out, not_13_out, not_14_out, not_15_out, not_16_out, not_17_out, not_18_out, x0);
  and and_3 (and_3_out, not_19_out, not_20_out, not_21_out, not_22_out, not_23_out, not_24_out, not_25_out, not_26_out, x1, not_27_out);
  and and_4 (and_4_out, not_28_out, not_29_out, not_30_out, not_31_out, not_32_out, not_33_out, x3, not_34_out, not_35_out, not_36_out);
  and and_5 (and_5_out, not_37_out, not_38_out, not_39_out, not_40_out, not_41_out, x4, not_42_out, not_43_out, not_44_out, not_45_out);
  and and_6 (and_6_out, not_46_out, not_47_out, not_48_out, not_49_out, x5, not_50_out, not_51_out, not_52_out, not_53_out, not_54_out);
  and and_7 (and_7_out, not_55_out, not_56_out, not_57_out, x6, not_58_out, not_59_out, not_60_out, not_61_out, not_62_out, not_63_out);
  and and_8 (and_8_out, not_64_out, not_65_out, x7, not_66_out, not_67_out, not_68_out, not_69_out, not_70_out, not_71_out, not_72_out);
  and and_9 (and_9_out, not_73_out, x8, not_74_out, not_75_out, not_76_out, not_77_out, not_78_out, not_79_out, not_80_out, not_81_out);
  and and_10 (and_10_out, x9, not_82_out, not_83_out, not_84_out, not_85_out, not_86_out, not_87_out, not_88_out, not_89_out, not_90_out);
  and and_11 (and_11_out, not_91_out, not_92_out, not_93_out, not_94_out, not_95_out, not_96_out, not_97_out, not_98_out, not_99_out, x0);
  and and_12 (and_12_out, not_100_out, not_101_out, not_102_out, not_103_out, not_104_out, not_105_out, not_106_out, x2, not_107_out, not_108_out);
  and and_13 (and_13_out, not_109_out, not_110_out, not_111_out, not_112_out, not_113_out, not_114_out, x3, not_115_out, not_116_out, not_117_out);
  and and_14 (and_14_out, not_118_out, not_119_out, not_120_out, not_121_out, x5, not_122_out, not_123_out, not_124_out, not_125_out, not_126_out);
  and and_15 (and_15_out, not_127_out, not_128_out, not_129_out, x6, not_130_out, not_131_out, not_132_out, not_133_out, not_134_out, not_135_out);
  and and_16 (and_16_out, not_136_out, x8, not_137_out, not_138_out, not_139_out, not_140_out, not_141_out, not_142_out, not_143_out, not_144_out);
  and and_17 (and_17_out, x9, not_145_out, not_146_out, not_147_out, not_148_out, not_149_out, not_150_out, not_151_out, not_152_out, not_153_out);
  and and_18 (and_18_out, not_154_out, not_155_out, not_156_out, not_157_out, not_158_out, not_159_out, not_160_out, not_161_out, not_162_out, x0);
  and and_19 (and_19_out, not_163_out, not_164_out, not_165_out, not_166_out, not_167_out, not_168_out, not_169_out, x2, not_170_out, not_171_out);
  and and_20 (and_20_out, not_172_out, not_173_out, not_174_out, x6, not_175_out, not_176_out, not_177_out, not_178_out, not_179_out, not_180_out);
  and and_21 (and_21_out, not_181_out, x8, not_182_out, not_183_out, not_184_out, not_185_out, not_186_out, not_187_out, not_188_out, not_189_out);
  and and_22 (and_22_out, not_190_out, not_191_out, not_192_out, not_193_out, not_194_out, not_195_out, not_196_out, x2, not_197_out, not_198_out);
  and and_23 (and_23_out, not_199_out, not_200_out, not_201_out, not_202_out, not_203_out, not_204_out, x3, not_205_out, not_206_out, not_207_out);
  and and_24 (and_24_out, not_208_out, not_209_out, not_210_out, not_211_out, not_212_out, x4, not_213_out, not_214_out, not_215_out, not_216_out);
  and and_25 (and_25_out, not_217_out, not_218_out, not_219_out, not_220_out, x5, not_221_out, not_222_out, not_223_out, not_224_out, not_225_out);
  and and_26 (and_26_out, not_226_out, not_227_out, not_228_out, x6, not_229_out, not_230_out, not_231_out, not_232_out, not_233_out, not_234_out);
  and and_27 (and_27_out, not_235_out, x8, not_236_out, not_237_out, not_238_out, not_239_out, not_240_out, not_241_out, not_242_out, not_243_out);
  and and_28 (and_28_out, x9, not_244_out, not_245_out, not_246_out, not_247_out, not_248_out, not_249_out, not_250_out, not_251_out, not_252_out);
  and and_29 (and_29_out, not_253_out, not_254_out, not_255_out, not_256_out, not_257_out, not_258_out, not_259_out, not_260_out, not_261_out, x0);
  and and_30 (and_30_out, not_262_out, not_263_out, not_264_out, not_265_out, not_266_out, x4, not_267_out, not_268_out, not_269_out, not_270_out);
  and and_31 (and_31_out, not_271_out, not_272_out, not_273_out, not_274_out, x5, not_275_out, not_276_out, not_277_out, not_278_out, not_279_out);
  and and_32 (and_32_out, not_280_out, not_281_out, not_282_out, x6, not_283_out, not_284_out, not_285_out, not_286_out, not_287_out, not_288_out);
  and and_33 (and_33_out, not_289_out, x8, not_290_out, not_291_out, not_292_out, not_293_out, not_294_out, not_295_out, not_296_out, not_297_out);
  and and_34 (and_34_out, x9, not_298_out, not_299_out, not_300_out, not_301_out, not_302_out, not_303_out, not_304_out, not_305_out, not_306_out);
  and and_35 (and_35_out, not_307_out, not_308_out, not_309_out, not_310_out, not_311_out, not_312_out, not_313_out, not_314_out, not_315_out, x0);
  and and_36 (and_36_out, not_316_out, not_317_out, not_318_out, not_319_out, not_320_out, not_321_out, not_322_out, x2, not_323_out, not_324_out);
  and and_37 (and_37_out, not_325_out, not_326_out, not_327_out, not_328_out, not_329_out, not_330_out, x3, not_331_out, not_332_out, not_333_out);
  and and_38 (and_38_out, not_334_out, not_335_out, not_336_out, not_337_out, x5, not_338_out, not_339_out, not_340_out, not_341_out, not_342_out);
  and and_39 (and_39_out, not_343_out, not_344_out, not_345_out, x6, not_346_out, not_347_out, not_348_out, not_349_out, not_350_out, not_351_out);
  and and_40 (and_40_out, not_352_out, not_353_out, x7, not_354_out, not_355_out, not_356_out, not_357_out, not_358_out, not_359_out, not_360_out);
  and and_41 (and_41_out, not_361_out, x8, not_362_out, not_363_out, not_364_out, not_365_out, not_366_out, not_367_out, not_368_out, not_369_out);
  and and_42 (and_42_out, x9, not_370_out, not_371_out, not_372_out, not_373_out, not_374_out, not_375_out, not_376_out, not_377_out, not_378_out);
  and and_43 (and_43_out, not_379_out, not_380_out, not_381_out, not_382_out, not_383_out, not_384_out, not_385_out, not_386_out, not_387_out, x0);
  and and_44 (and_44_out, not_388_out, not_389_out, not_390_out, not_391_out, not_392_out, not_393_out, not_394_out, x1, not_395_out);
  and and_45 (and_45_out, not_396_out, not_397_out, not_398_out, not_399_out, not_400_out, not_401_out, not_402_out, x2, not_403_out, not_404_out);
  and and_46 (and_46_out, not_405_out, not_406_out, not_407_out, not_408_out, not_409_out, not_410_out, x3, not_411_out, not_412_out, not_413_out);
  and and_47 (and_47_out, not_414_out, not_415_out, not_416_out, not_417_out, not_418_out, x4, not_419_out, not_420_out, not_421_out, not_422_out);
  and and_48 (and_48_out, not_423_out, not_424_out, x7, not_425_out, not_426_out, not_427_out, not_428_out, not_429_out, not_430_out, not_431_out);
  and and_49 (and_49_out, not_432_out, x8, not_433_out, not_434_out, not_435_out, not_436_out, not_437_out, not_438_out, not_439_out, not_440_out);
  and and_50 (and_50_out, not_441_out, x8, not_442_out, not_443_out, x5, x4, not_444_out, not_445_out, x1, not_446_out);
  and and_51 (and_51_out, x9, not_447_out, not_448_out, not_449_out, not_450_out, not_451_out, not_452_out, not_453_out, not_454_out, not_455_out);
  and and_52 (and_52_out, not_456_out, not_457_out, not_458_out, not_459_out, not_460_out, not_461_out, not_462_out, not_463_out, not_464_out, not_465_out);
  and and_53 (and_53_out, x1, x0);
  and and_54 (and_54_out, x2, x0);
  and and_55 (and_55_out, x2, x1);
  and and_56 (and_56_out, x3, x0);
  and and_57 (and_57_out, x3, x1);
  and and_58 (and_58_out, x3, x2);
  and and_59 (and_59_out, x4, x0);
  not not_468 (not_468_out, x5);
  and and_60 (and_60_out, not_468_out, x4, x1);
  and and_61 (and_61_out, x4, x2);
  and and_62 (and_62_out, x4, x3);
  and and_63 (and_63_out, x5, x0);
  not not_469 (not_469_out, x8);
  and and_64 (and_64_out, not_469_out, x5, x1);
  not not_470 (not_470_out, x6);
  and and_65 (and_65_out, not_470_out, x5, x2);
  and and_66 (and_66_out, x5, x3);
  and and_67 (and_67_out, x5, x4, not_471_out);
  not not_471 (not_471_out, x1);
  and and_68 (and_68_out, x6, x0);
  and and_69 (and_69_out, x6, x1);
  and and_70 (and_70_out, x6, x3);
  and and_71 (and_71_out, x6, x4);
  not not_472 (not_472_out, x8);
  and and_72 (and_72_out, not_472_out, x6, x5);
  and and_73 (and_73_out, x7, x0);
  and and_74 (and_74_out, x7, x1);
  and and_75 (and_75_out, x7, x2);
  and and_76 (and_76_out, x7, x3);
  and and_77 (and_77_out, x7, x4);
  and and_78 (and_78_out, x7, x5);
  and and_79 (and_79_out, x7, x6);
  and and_80 (and_80_out, x8, x0);
  and and_81 (and_81_out, x8, not_473_out, x1);
  not not_473 (not_473_out, x5);
  and and_82 (and_82_out, x8, not_474_out, x2);
  not not_474 (not_474_out, x5);
  and and_83 (and_83_out, x8, x3);
  not not_475 (not_475_out, x5);
  and and_84 (and_84_out, x8, not_475_out, x4);
  and and_85 (and_85_out, x8, not_466_out, x5, not_467_out);
  and and_86 (and_86_out, x8, x6, not_476_out);
  not not_476 (not_476_out, x2);
  and and_87 (and_87_out, x8, x7);
  and and_88 (and_88_out, x9, x0);
  and and_89 (and_89_out, x9, x1);
  and and_90 (and_90_out, x9, x2);
  and and_91 (and_91_out, x9, x3);
  and and_92 (and_92_out, x9, x4);
  and and_93 (and_93_out, x9, x5);
  and and_94 (and_94_out, x9, x6);
  and and_95 (and_95_out, x9, x7);
  and and_96 (and_96_out, x9, x8);
  or or_1 (y4, and_18_out, and_19_out, and_20_out, and_21_out);
  or or_2 (y6, and_2_out, and_3_out, and_4_out, and_5_out, and_6_out, and_7_out, and_8_out, and_9_out, and_10_out);
  or or_3 (y5, and_11_out, and_12_out, and_13_out, and_14_out, and_15_out, and_16_out, and_17_out);
  or or_4 (y3, and_22_out, and_23_out, and_24_out, and_25_out, and_26_out, and_27_out, and_28_out);
  or or_5 (y2, and_29_out, and_30_out, and_31_out, and_32_out, and_33_out, and_34_out);
  or or_6 (y1, and_35_out, and_36_out, and_37_out, and_38_out, and_39_out, and_40_out, and_41_out, and_42_out);
  or or_7 (y0, and_43_out, and_44_out, and_45_out, and_46_out, and_47_out, and_48_out, and_49_out, and_50_out, and_51_out);
  or or_8 (or_8_out, and_52_out, and_53_out, and_54_out, and_55_out, and_56_out, and_57_out, and_58_out, and_59_out, and_60_out, and_61_out, and_62_out, and_63_out, and_64_out, and_65_out, and_66_out, and_67_out, and_68_out, and_69_out, and_70_out, and_71_out, and_72_out, and_73_out, and_74_out);
  or or_9 (ERROR, or_8_out, or_10_out);
  or or_10 (or_10_out, and_75_out, and_76_out, and_77_out, and_78_out, and_79_out, and_80_out, and_81_out, and_82_out, and_83_out, and_84_out, and_85_out, and_86_out, and_87_out, and_88_out, and_89_out, and_90_out, and_91_out, and_92_out, and_93_out, and_94_out, and_95_out, and_96_out);
endmodule

module \_7сегментов  (
  input  _9,
  input  _8,
  input  _7,
  input  _6,
  input  _5,
  input  _4,
  input  _3,
  input  _2,
  input  _1,
  input  _0,
  output ERROR
);

  wire \дешифратор_1_y0 , \дешифратор_1_y1 , \дешифратор_1_y2 , \дешифратор_1_y3 , \дешифратор_1_y4 ,
       \дешифратор_1_y5 , \дешифратор_1_y6 , \дешифратор_1_y7 ;

  \дешифратор  \u_дешифратор_1  (
    .x9(_9), .x8(_8), .x7(_7), .y7(\дешифратор_1_y7 ), .x6(_6), .x5(_5), .x4(_4), .x3(_3), .x2(_2), .x1(_1),
    .x0(_0), .y6(\дешифратор_1_y6 ), .y4(\дешифратор_1_y4 ), .y3(\дешифратор_1_y3 ), .y2(\дешифратор_1_y2 ),
    .y1(\дешифратор_1_y1 ), .y0(\дешифратор_1_y0 ), .ERROR(ERROR), .y5(\дешифратор_1_y5 ));
  _7_Segment_Display u_7_segment_display_1 (
    .g(\дешифратор_1_y3 ), .f(\дешифратор_1_y2 ), .a(\дешифратор_1_y1 ), .b(\дешифратор_1_y0 ),
    .e(\дешифратор_1_y4 ), .d(\дешифратор_1_y5 ), .c(\дешифратор_1_y6 ), .dp(\дешифратор_1_y7 ));
endmodule

module \_16сегментов  (
  input  x7,
  input  x6,
  input  x5,
  input  x4,
  input  x3,
  input  x2,
  input  x1,
  input  x0,
  output y3,
  output y2,
  output y1,
  output y0
);

  wire and_1_out, and_2_out, and_3_out, and_4_out, and_5_out, and_6_out, and_7_out, and_8_out, and_9_out,
       and_10_out, and_11_out, and_12_out, not_1_out, not_2_out, not_3_out, not_4_out, not_5_out, not_6_out,
       not_7_out, not_8_out, not_9_out, not_10_out, not_11_out, not_12_out;

  not not_1 (not_1_out, x6);
  and and_1 (and_1_out, not_1_out, not_2_out);
  not not_2 (not_2_out, x4);
  and and_2 (and_2_out, x3, x2, x1, x0);
  and and_3 (and_3_out, x4, x3, not_3_out);
  not not_3 (not_3_out, x1);
  and and_4 (and_4_out, x6, not_4_out);
  not not_4 (not_4_out, x0);
  and and_5 (and_5_out, x6, not_5_out, x1);
  not not_5 (not_5_out, x5);
  and and_6 (and_6_out, x6, x2, not_6_out);
  not not_6 (not_6_out, x1);
  not not_7 (not_7_out, x1);
  not not_8 (not_8_out, x2);
  not not_9 (not_9_out, x2);
  not not_10 (not_10_out, x1);
  not not_11 (not_11_out, x2);
  not not_12 (not_12_out, x4);
  or or_1 (y3, and_1_out, and_2_out);
  or or_2 (y2, and_3_out, and_4_out, and_5_out, and_6_out);
  and and_7 (and_7_out, x4, x2, not_7_out, x0);
  and and_8 (and_8_out, x5, not_8_out);
  and and_9 (and_9_out, x6, not_9_out, x1);
  and and_10 (and_10_out, x4, x2, not_10_out, x0);
  and and_11 (and_11_out, x6, not_11_out);
  or or_3 (y0, and_10_out, and_11_out, and_12_out);
  and and_12 (and_12_out, x6, not_12_out, x1);
  or or_4 (y1, and_7_out, and_8_out, and_9_out, x7);
endmodule

module \мультиплексор  (
  input  in_1,
  input  in_2,
  input  in_3,
  input  in_4,
  input  in_5,
  input  in_6,
  input  in_7,
  input  in_8,
  input  in_9,
  input  in_10,
  input  in_11,
  output out_12
);

  wire and_1_out, and_2_out, and_3_out, and_4_out, and_5_out, and_6_out, and_7_out, and_8_out, and_9_out,
       and_10_out, and_11_out, and_12_out, and_13_out, and_14_out, and_15_out, and_16_out, not_1_out,
       not_2_out, not_3_out;

  not not_1 (not_1_out, in_11);
  not not_2 (not_2_out, in_10);
  not not_3 (not_3_out, in_9);
  and and_1 (and_1_out, in_1, and_3_out);
  and and_2 (and_2_out, in_2, and_4_out);
  and and_3 (and_3_out, not_1_out, not_2_out, not_3_out);
  and and_4 (and_4_out, not_2_out, not_1_out, in_9);
  and and_5 (and_5_out, not_3_out, not_1_out, in_10);
  and and_6 (and_6_out, in_9, in_10, not_1_out);
  and and_7 (and_7_out, not_3_out, not_2_out, in_11);
  and and_8 (and_8_out, in_9, not_2_out, in_11);
  and and_9 (and_9_out, not_3_out, in_10, in_11);
  and and_10 (and_10_out, in_9, in_10, in_11);
  and and_11 (and_11_out, in_3, and_5_out);
  and and_12 (and_12_out, in_4, and_6_out);
  and and_13 (and_13_out, in_5, and_7_out);
  and and_14 (and_14_out, in_6, and_8_out);
  and and_15 (and_15_out, in_7, and_9_out);
  and and_16 (and_16_out, in_8, and_10_out);
  or or_1 (out_12, and_1_out, and_2_out, and_11_out, and_12_out, and_13_out, and_14_out, and_15_out, and_16_out);
endmodule

module \_4_мультиплексор  (
  input  in_1,
  input  in_2,
  input  in_3,
  input  in_4,
  input  in_5,
  input  in_6,
  input  in_7,
  input  in_8,
  input  in_9,
  input  in_10,
  input  in_11,
  output out_12
);

  \мультиплексор  \u_мультиплексор_1  (
    .in_1(in_1), .in_2(in_2), .in_3(in_3), .in_4(in_4), .in_5(in_5), .in_6(in_6), .in_7(in_7), .in_8(in_8),
    .in_9(in_11), .in_10(in_10), .in_11(in_9), .out_12(out_12));
endmodule

module \демультиплексор  (
  input  in_1,
  input  in_2,
  input  in_3,
  input  in_4,
  output out_5,
  output out_6,
  output out_7,
  output out_8,
  output out_9,
  output out_10,
  output out_11,
  output out_12
);

  wire and_3_out, and_4_out, and_5_out, and_6_out, and_7_out, and_8_out, and_9_out, and_10_out, not_1_out,
       not_2_out, not_3_out;

  not not_1 (not_1_out, in_4);
  not not_2 (not_2_out, in_3);
  not not_3 (not_3_out, in_2);
  and and_1 (out_5, in_1, and_3_out);
  and and_2 (out_6, in_1, and_4_out);
  and and_3 (and_3_out, not_1_out, not_2_out, not_3_out);
  and and_4 (and_4_out, not_2_out, not_1_out, in_2);
  and and_5 (and_5_out, not_3_out, not_1_out, in_3);
  and and_6 (and_6_out, in_2, in_3, not_1_out);
  and and_7 (and_7_out, not_3_out, not_2_out, in_4);
  and and_8 (and_8_out, in_2, not_2_out, in_4);
  and and_9 (and_9_out, not_3_out, in_3, in_4);
  and and_10 (and_10_out, in_2, in_3, in_4);
  and and_11 (out_7, in_1, and_5_out);
  and and_12 (out_8, in_1, and_6_out);
  and and_13 (out_9, in_1, and_7_out);
  and and_14 (out_10, in_1, and_8_out);
  and and_15 (out_11, in_1, and_9_out);
  and and_16 (out_12, in_1, and_10_out);
endmodule

module \_4_демультиплексор  (
  input  in_1,
  input  in_2,
  input  in_3,
  input  in_4,
  output out_5,
  output out_6,
  output out_7,
  output out_8,
  output out_9,
  output out_10,
  output out_11,
  output out_12
);

  \демультиплексор  \u_демультиплексор_1  (
    .in_1(in_1), .in_2(in_4), .in_3(in_3), .in_4(in_2), .out_5(out_5), .out_6(out_6), .out_7(out_7),
    .out_8(out_8), .out_9(out_9), .out_10(out_10), .out_11(out_11), .out_12(out_12));
endmodule

module \дешифратор_3  (
  input  x3,
  input  x2,
  input  x1,
  input  x0,
  output y0,
  output y1,
  output y2,
  output y3,
  output y4,
  output y5,
  output y6,
  output y7
);

  wire and_1_out, and_2_out, and_3_out, and_4_out, and_5_out, and_6_out, and_7_out, and_8_out, and_9_out,
       and_10_out, and_11_out, and_12_out, and_13_out, and_14_out, and_15_out, and_16_out, and_17_out,
       and_18_out, and_19_out, and_20_out, and_21_out, and_22_out, and_23_out, and_24_out, and_25_out,
       and_26_out, and_27_out, and_28_out, and_29_out, and_30_out, and_31_out, and_32_out, and_33_out,
       and_34_out, and_35_out, and_36_out, and_37_out, and_38_out, not_1_out, not_2_out, not_3_out,
       not_4_out, not_5_out, not_6_out, not_7_out, not_8_out, not_9_out, not_10_out, not_11_out, not_12_out,
       not_13_out, not_14_out, not_15_out, not_16_out, not_17_out, not_18_out, not_19_out, not_20_out,
       not_21_out, not_22_out, not_23_out, not_24_out, not_25_out, not_26_out, not_27_out, not_28_out,
       not_29_out, not_30_out, not_31_out, not_32_out, not_33_out, not_34_out, not_35_out, not_36_out,
       not_37_out, not_38_out, not_39_out, not_40_out, not_41_out, not_42_out, not_43_out, not_44_out,
       not_45_out, not_46_out, not_47_out, not_48_out, not_49_out;

  not not_1 (not_1_out, x3);
  not not_2 (not_2_out, x0);
  not not_3 (not_3_out, x2);
  not not_4 (not_4_out, x1);
  not not_5 (not_5_out, x3);
  and and_1 (and_1_out, not_5_out, not_6_out);
  not not_6 (not_6_out, x1);
  not not_7 (not_7_out, x3);
  and and_2 (and_2_out, not_7_out, x0);
  not not_8 (not_8_out, x1);
  and and_3 (and_3_out, not_8_out, x0);
  not not_9 (not_9_out, x3);
  and and_4 (and_4_out, not_9_out, x2);
  and and_5 (and_5_out, x3, not_10_out);
  not not_10 (not_10_out, x2);
  not not_11 (not_11_out, x3);
  not not_12 (not_12_out, x2);
  and and_6 (and_6_out, not_11_out, not_12_out, not_13_out);
  not not_13 (not_13_out, x0);
  not not_14 (not_14_out, x2);
  and and_7 (and_7_out, not_14_out, x1, x0);
  not not_15 (not_15_out, x1);
  and and_8 (and_8_out, x2, not_15_out, x0);
  and and_9 (and_9_out, x2, x1, not_16_out);
  not not_16 (not_16_out, x0);
  and and_10 (and_10_out, x3, not_17_out);
  not not_17 (not_17_out, x1);
  not not_18 (not_18_out, x2);
  and and_11 (and_11_out, not_18_out, not_19_out);
  not not_19 (not_19_out, x0);
  and and_12 (and_12_out, x1, not_20_out);
  not not_20 (not_20_out, x0);
  and and_13 (and_13_out, x3, x1);
  and and_14 (and_14_out, x3, x2);
  not not_21 (not_21_out, x2);
  and and_15 (and_15_out, not_21_out, x1);
  and and_16 (and_16_out, x1, not_22_out);
  not not_22 (not_22_out, x0);
  not not_23 (not_23_out, x3);
  and and_17 (and_17_out, not_23_out, x2, not_24_out);
  not not_24 (not_24_out, x1);
  and and_18 (and_18_out, x3, not_25_out);
  not not_25 (not_25_out, x2);
  and and_19 (and_19_out, x3, x0);
  not not_26 (not_26_out, x1);
  and and_20 (and_20_out, not_26_out, not_27_out);
  not not_27 (not_27_out, x0);
  not not_28 (not_28_out, x3);
  and and_21 (and_21_out, not_28_out, x2, not_29_out);
  not not_29 (not_29_out, x1);
  and and_22 (and_22_out, x2, not_30_out);
  not not_30 (not_30_out, x0);
  and and_23 (and_23_out, x3, not_31_out);
  not not_31 (not_31_out, x2);
  and and_24 (and_24_out, x3, x1);
  not not_32 (not_32_out, x2);
  and and_25 (and_25_out, not_32_out, not_33_out);
  not not_33 (not_33_out, x0);
  not not_34 (not_34_out, x3);
  and and_26 (and_26_out, not_34_out, x1);
  not not_35 (not_35_out, x3);
  and and_27 (and_27_out, not_35_out, x2, x0);
  and and_28 (and_28_out, x2, x1);
  and and_29 (and_29_out, x3, not_36_out, not_37_out);
  not not_36 (not_36_out, x2);
  not not_37 (not_37_out, x1);
  and and_30 (and_30_out, x3, not_38_out);
  not not_38 (not_38_out, x0);
  not not_39 (not_39_out, x3);
  and and_31 (and_31_out, not_39_out, not_40_out);
  not not_40 (not_40_out, x2);
  not not_41 (not_41_out, x3);
  and and_32 (and_32_out, not_41_out, not_42_out, not_43_out);
  not not_42 (not_42_out, x1);
  not not_43 (not_43_out, x0);
  not not_44 (not_44_out, x2);
  and and_33 (and_33_out, not_44_out, not_45_out);
  not not_45 (not_45_out, x1);
  not not_46 (not_46_out, x2);
  and and_34 (and_34_out, not_46_out, not_47_out);
  not not_47 (not_47_out, x0);
  not not_48 (not_48_out, x3);
  and and_35 (and_35_out, not_48_out, x1, x0);
  not not_49 (not_49_out, x1);
  and and_36 (and_36_out, x3, not_49_out, x0);
  and and_37 (and_37_out, not_1_out, x2, x1, not_2_out);
  or or_1 (y0, and_37_out, and_38_out);
  and and_38 (and_38_out, x3, not_3_out, not_4_out, x0);
  or or_2 (y1, and_1_out, and_2_out, and_3_out, and_4_out, and_5_out);
  or or_3 (y2, and_6_out, and_7_out, and_8_out, and_9_out, and_10_out);
  or or_4 (y3, and_11_out, and_12_out, and_13_out, and_14_out);
  or or_5 (y4, and_15_out, and_16_out, and_17_out, and_18_out, and_19_out);
  or or_6 (y5, and_20_out, and_21_out, and_22_out, and_23_out, and_24_out);
  or or_7 (y6, and_25_out, and_26_out, and_27_out, and_28_out, and_29_out, and_30_out);
  or or_8 (y7, and_31_out, and_32_out, and_33_out, and_34_out, and_35_out, and_36_out);
endmodule

module \_3_задание  (
  input  _0,
  input  in_2,
  input  in_3,
  input  in_4,
  input  in_5,
  input  in_6,
  input  in_7,
  input  _7
);

  wire \дешифратор_3_1_y0 , \дешифратор_3_1_y1 , \дешифратор_3_1_y2 , \дешифратор_3_1_y3 ,
       \дешифратор_3_1_y4 , \дешифратор_3_1_y5 , \дешифратор_3_1_y6 , \дешифратор_3_1_y7 , \шифратор_3_1_y0 ,
       \шифратор_3_1_y1 , \шифратор_3_1_y2 , \шифратор_3_1_y3 ;

  \шифратор_3  \u_шифратор_3_1  (
    .x0(_0), .x1(in_2), .x2(in_3), .y0(\шифратор_3_1_y0 ), .x3(in_4), .x4(in_5), .x5(in_6), .x6(in_7),
    .x7(_7), .y1(\шифратор_3_1_y1 ), .y2(\шифратор_3_1_y2 ), .y3(\шифратор_3_1_y3 ));
  \дешифратор_3  \u_дешифратор_3_1  (
    .x3(\шифратор_3_1_y0 ), .x2(\шифратор_3_1_y1 ), .x1(\шифратор_3_1_y2 ), .x0(\шифратор_3_1_y3 ),
    .y0(\дешифратор_3_1_y0 ), .y1(\дешифратор_3_1_y1 ), .y2(\дешифратор_3_1_y2 ), .y3(\дешифратор_3_1_y3 ),
    .y4(\дешифратор_3_1_y4 ), .y5(\дешифратор_3_1_y5 ), .y6(\дешифратор_3_1_y6 ), .y7(\дешифратор_3_1_y7 ));
  _7_Segment_Display u_7_segment_display_1 (
    .g(\дешифратор_3_1_y4 ), .f(\дешифратор_3_1_y5 ), .a(\дешифратор_3_1_y6 ), .b(\дешифратор_3_1_y7 ),
    .e(\дешифратор_3_1_y3 ), .d(\дешифратор_3_1_y2 ), .c(\дешифратор_3_1_y1 ), .dp(\дешифратор_3_1_y0 ));
endmodule

module \шифратор_3  (
  input  x0,
  input  x1,
  input  x2,
  input  x3,
  input  x4,
  input  x5,
  input  x6,
  input  x7,
  output y0,
  output y1,
  output y2,
  output y3
);

  wire and_1_out, and_2_out, and_3_out, and_4_out, and_5_out, and_6_out, and_7_out, and_8_out, and_9_out,
       and_10_out, and_11_out, and_12_out, and_13_out, and_14_out, and_15_out, and_16_out, not_1_out,
       not_2_out, not_3_out, not_4_out, not_5_out, not_6_out, not_7_out, not_8_out, not_9_out, not_10_out,
       not_11_out, not_12_out, not_13_out, not_14_out, not_15_out, not_16_out, not_17_out, not_18_out,
       not_19_out, not_20_out, not_21_out, not_22_out;

  not not_1 (not_1_out, x4);
  not not_2 (not_2_out, x7);
  not not_3 (not_3_out, x0);
  not not_4 (not_4_out, x6);
  not not_5 (not_5_out, x3);
  not not_6 (not_6_out, x2);
  not not_7 (not_7_out, x3);
  and and_1 (and_1_out, not_6_out, not_7_out, x6);
  and and_2 (and_2_out, x6, not_8_out);
  not not_8 (not_8_out, x7);
  not not_9 (not_9_out, x2);
  not not_10 (not_10_out, x3);
  and and_3 (and_3_out, not_9_out, not_10_out, x5);
  and and_4 (and_4_out, x3, not_11_out, not_12_out);
  not not_11 (not_11_out, x5);
  not not_12 (not_12_out, x6);
  not not_13 (not_13_out, x2);
  and and_5 (and_5_out, not_13_out, x6);
  not not_14 (not_14_out, x5);
  and and_6 (and_6_out, not_14_out, x6);
  and and_7 (and_7_out, x3, not_15_out, not_16_out);
  not not_15 (not_15_out, x4);
  not not_16 (not_16_out, x6);
  and and_8 (and_8_out, x3, x4, not_17_out);
  not not_17 (not_17_out, x7);
  not not_18 (not_18_out, x2);
  and and_9 (and_9_out, not_18_out, not_19_out);
  not not_19 (not_19_out, x7);
  not not_20 (not_20_out, x3);
  and and_10 (and_10_out, not_20_out, x6);
  and and_11 (and_11_out, x2, not_21_out);
  not not_21 (not_21_out, x6);
  and and_12 (and_12_out, x1, not_22_out);
  not not_22 (not_22_out, x5);
  and and_13 (and_13_out, not_1_out, not_2_out);
  and and_14 (and_14_out, not_3_out, x3, x4, x5);
  and and_15 (and_15_out, x2, not_4_out);
  and and_16 (and_16_out, x2, not_5_out, x5, x7);
  or or_1 (y1, and_1_out, and_2_out, and_3_out, and_4_out);
  or or_2 (y2, and_5_out, and_6_out, and_7_out, and_8_out);
  or or_3 (y3, and_9_out, and_10_out, and_11_out, and_12_out);
  or or_4 (y0, and_13_out, and_14_out, and_15_out, and_16_out);
endmodule
