// Logisim project сумматор (1).circ as structural Verilog: 7 circuits, main circuit полусумматор
module \Сумматор  (
  input  CI,
  input  A,
  input  B,
  output S,
  output CO
);

  wire \полусумматор_1_carry , \полусумматор_1_sum , \полусумматор_2_carry ;

  \полусумматор  \u_полусумматор_1  (.A(A), .B(B), .SUM(\полусумматор_1_sum ), .CARRY(\полусумматор_1_carry ));
  \полусумматор  \u_полусумматор_2  (.A(CI), .B(\полусумматор_1_sum ), .SUM(S), .CARRY(\полусумматор_2_carry ));
  or or_1 (CO, \полусумматор_2_carry , \полусумматор_1_carry );
endmodule

module \полусумматор  (
  input  A,
  input  B,
  output SUM,
  output CARRY
);

  and and_1 (CARRY, A, B);
  xor xor_1 (SUM, A, B);
endmodule

module \сумматор_двухбитный  (
  input  A,
  input  in_2,
  input  in_3,
  input  in_4,
  output out_5,
  output out_6,
  output out_7
);

  wire \сумматор_2_co ;

  \Сумматор  \u_сумматор_1  (.CI(\сумматор_2_co ), .A(A), .B(in_3), .S(out_6), .CO(out_5));
  \Сумматор  \u_сумматор_2  (.CI(1'b0), .A(in_2), .B(in_4), .S(out_7), .CO(\сумматор_2_co ));

  // Notes on the sheet:
  //   +
  //   B
endmodule

module \сумматор_восьмибитный  (
  input  in_1,
  input  in_2,
  input  in_3,
  input  in_4,
  input  in_5,
  input  in_6,
  input  in_7,
  input  in_8,
  input  in_9,
  input  in_10,
  input  in_11,
  input  in_12,
  input  in_13,
  input  in_14,
  input  in_15,
  input  in_16,
  output out_17,
  output out_18,
  output out_19,
  output out_20,
  output out_21,
  output out_22,
  output out_23,
  output out_24,
  output out_25
);

  wire \сумматор_2_co , \сумматор_3_co , \сумматор_4_co , \сумматор_5_co , \сумматор_6_co , \сумматор_7_co ,
       \сумматор_8_co ;

  \Сумматор  \u_сумматор_1  (.CI(\сумматор_2_co ), .A(in_1), .B(in_9), .S(out_18), .CO(out_17));
  \Сумматор  \u_сумматор_2  (.CI(\сумматор_3_co ), .A(in_2), .B(in_10), .S(out_19), .CO(\сумматор_2_co ));
  \Сумматор  \u_сумматор_3  (.CI(\сумматор_4_co ), .A(in_3), .B(in_11), .S(out_20), .CO(\сумматор_3_co ));
  \Сумматор  \u_сумматор_4  (.CI(\сумматор_5_co ), .A(in_4), .B(in_12), .S(out_21), .CO(\сумматор_4_co ));
  \Сумматор  \u_сумматор_5  (.CI(\сумматор_6_co ), .A(in_5), .B(in_13), .S(out_22), .CO(\сумматор_5_co ));
  \Сумматор  \u_сумматор_6  (.CI(\сумматор_7_co ), .A(in_6), .B(in_14), .S(out_23), .CO(\сумматор_6_co ));
  \Сумматор  \u_сумматор_7  (.CI(\сумматор_8_co ), .A(in_7), .B(in_15), .S(out_24), .CO(\сумматор_7_co ));
  \Сумматор  \u_сумматор_8  (.CI(1'b0), .A(in_8), .B(in_16), .S(out_25), .CO(\сумматор_8_co ));
endmodule

module \не  (
  input  in_1,
  output out_2
);

  Transistor transistor_1 (.in(1'b1), .out(out_2), .gate(in_1));
  Transistor #(.\type ("n")) transistor_2 (.in(1'b0), .out(out_2), .gate(in_1));
endmodule

module \вычитатор  (
  input  in_1,
  input  in_2,
  input  in_3,
  input  in_4,
  input  in_5,
  input  in_6,
  input  in_7,
  input  in_8,
  input  in_9,
  input  in_10,
  input  in_11,
  input  in_12,
  input  in_13,
  input  in_14,
  input  in_15,
  input  in_16,
  output out_17,
  output out_18,
  output out_19,
  output out_20,
  output out_21,
  output out_22,
  output out_23,
  output out_24,
  output out_25
);

  wire \сумматор_2_co , \сумматор_3_co , \сумматор_4_co , \сумматор_5_co , \сумматор_6_co , \сумматор_7_co ,
       \сумматор_8_co ;

  \Сумматор  \u_сумматор_1  (.CI(\сумматор_2_co ), .A(in_1), .B(in_9), .S(out_18), .CO(out_17));
  \Сумматор  \u_сумматор_2  (.CI(\сумматор_3_co ), .A(in_2), .B(in_10), .S(out_19), .CO(\сумматор_2_co ));
  \Сумматор  \u_сумматор_3  (.CI(\сумматор_4_co ), .A(in_3), .B(in_11), .S(out_20), .CO(\сумматор_3_co ));
  \Сумматор  \u_сумматор_4  (.CI(\сумматор_5_co ), .A(in_4), .B(in_12), .S(out_21), .CO(\сумматор_4_co ));
  \Сумматор  \u_сумматор_5  (.CI(\сумматор_6_co ), .A(in_5), .B(in_13), .S(out_22), .CO(\сумматор_5_co ));
  \Сумматор  \u_сумматор_6  (.CI(\сумматор_7_co ), .A(in_6), .B(in_14), .S(out_23), .CO(\сумматор_6_co ));
  \Сумматор  \u_сумматор_7  (.CI(\сумматор_8_co ), .A(in_7), .B(in_15), .S(out_24), .CO(\сумматор_7_co ));
  \Сумматор  \u_сумматор_8  (.CI(1'b0), .A(in_8), .B(in_16), .S(out_25), .CO(\сумматор_8_co ));
endmodule

module \полувычитатор  (
  input  in_1,
  input  in_2,
  output out_3
);

  xor xor_1 (out_3, in_1, in_2);
endmodule
